// Logisim project 164_encoder.circ as structural Verilog: 5 circuits, main circuit main
module main (
);

  wire A0_out, A1_out, A2_out, A3_out, dipswitch_1_p1, dipswitch_1_p2, dipswitch_1_p3, dipswitch_1_p4,
       dipswitch_1_p5, dipswitch_1_p6, dipswitch_1_p7, dipswitch_1_p8, dipswitch_1_p9, dipswitch_1_p10,
       dipswitch_1_p11, dipswitch_1_p12, dipswitch_1_p13, dipswitch_1_p14, dipswitch_1_p15, seg7_test02_1_ya,
       seg7_test02_1_yb, seg7_test02_1_yc, seg7_test02_1_yd, seg7_test02_1_ye, seg7_test02_1_yf,
       seg7_test02_1_yg;

  // DipSwitch #(.number(16)) dipswitch_1: pin names not known; wires that end beside it: dipswitch_1_p1, dipswitch_1_p2, dipswitch_1_p3, dipswitch_1_p4, dipswitch_1_p5, dipswitch_1_p6, dipswitch_1_p7, dipswitch_1_p8, dipswitch_1_p9, dipswitch_1_p10, dipswitch_1_p11, dipswitch_1_p12, dipswitch_1_p13, dipswitch_1_p14, dipswitch_1_p15
  or A0 (A0_out, dipswitch_1_p1, dipswitch_1_p3, dipswitch_1_p5, dipswitch_1_p7, dipswitch_1_p9, dipswitch_1_p11, dipswitch_1_p13, dipswitch_1_p15);
  or A1 (A1_out, dipswitch_1_p2, dipswitch_1_p3, dipswitch_1_p6, dipswitch_1_p7, dipswitch_1_p10, dipswitch_1_p11, dipswitch_1_p14, dipswitch_1_p15);
  or A2 (A2_out, dipswitch_1_p4, dipswitch_1_p5, dipswitch_1_p6, dipswitch_1_p7, dipswitch_1_p12, dipswitch_1_p13, dipswitch_1_p14, dipswitch_1_p15);
  or A3 (A3_out, dipswitch_1_p8, dipswitch_1_p9, dipswitch_1_p10, dipswitch_1_p11, dipswitch_1_p12, dipswitch_1_p13, dipswitch_1_p14, dipswitch_1_p15);
  Seg7_test02 seg7_test02_1 (
    .A0(A0_out), .A1(A1_out), .A2(A2_out), .A3(A3_out), .Yg(seg7_test02_1_yg), .Yf(seg7_test02_1_yf),
    .Ya(seg7_test02_1_ya), .Yb(seg7_test02_1_yb), .Yc(seg7_test02_1_yc), .Yd(seg7_test02_1_yd),
    .Ye(seg7_test02_1_ye));
  _7_Segment_Display u_7_segment_display_1 (
    .g(seg7_test02_1_yg), .f(seg7_test02_1_yf), .a(seg7_test02_1_ya), .b(seg7_test02_1_yb),
    .e(seg7_test02_1_ye), .d(seg7_test02_1_yd), .c(seg7_test02_1_yc));  // open: dp
endmodule

module Seg7_test02 (
  input  A0,
  input  A1,
  input  A2,
  input  A3,
  output Yg,
  output Yf,
  output Ya,
  output Yb,
  output Yc,
  output Yd,
  output Ye
);

  wire decoder_416_1_y0, decoder_416_1_y1, decoder_416_1_y2, decoder_416_1_y3, decoder_416_1_y4,
       decoder_416_1_y5, decoder_416_1_y6, decoder_416_1_y7, decoder_416_1_y8, decoder_416_1_y9,
       decoder_416_1_y10, decoder_416_1_y11, decoder_416_1_y12, decoder_416_1_y13, decoder_416_1_y14,
       decoder_416_1_y15;

  decoder_416 decoder_416_1 (
    .A0(A0), .A1(A1), .A2(A2), .A3(A3), .Y0(decoder_416_1_y0), .Y1(decoder_416_1_y1), .Y2(decoder_416_1_y2),
    .Y3(decoder_416_1_y3), .Y4(decoder_416_1_y4), .Y5(decoder_416_1_y5), .Y6(decoder_416_1_y6),
    .Y7(decoder_416_1_y7), .Y8(decoder_416_1_y8), .Y9(decoder_416_1_y9), .Y10(decoder_416_1_y10),
    .Y11(decoder_416_1_y11), .Y12(decoder_416_1_y12), .Y13(decoder_416_1_y13), .Y14(decoder_416_1_y14),
    .Y15(decoder_416_1_y15));
  or g (Yg, decoder_416_1_y2, decoder_416_1_y3, decoder_416_1_y4, decoder_416_1_y5, decoder_416_1_y6, decoder_416_1_y8, decoder_416_1_y9, decoder_416_1_y10, decoder_416_1_y11, decoder_416_1_y13, decoder_416_1_y14, decoder_416_1_y15);
  or f (Yf, decoder_416_1_y0, decoder_416_1_y4, decoder_416_1_y5, decoder_416_1_y6, decoder_416_1_y8, decoder_416_1_y9, decoder_416_1_y10, decoder_416_1_y11, decoder_416_1_y12, decoder_416_1_y14, decoder_416_1_y15);
  or a (Ya, decoder_416_1_y0, decoder_416_1_y2, decoder_416_1_y3, decoder_416_1_y5, decoder_416_1_y6, decoder_416_1_y7, decoder_416_1_y8, decoder_416_1_y9, decoder_416_1_y10, decoder_416_1_y12, decoder_416_1_y14, decoder_416_1_y15);
  or b (Yb, decoder_416_1_y0, decoder_416_1_y1, decoder_416_1_y2, decoder_416_1_y3, decoder_416_1_y4, decoder_416_1_y7, decoder_416_1_y8, decoder_416_1_y9, decoder_416_1_y10, decoder_416_1_y13);
  or c (Yc, decoder_416_1_y0, decoder_416_1_y1, decoder_416_1_y3, decoder_416_1_y4, decoder_416_1_y5, decoder_416_1_y6, decoder_416_1_y7, decoder_416_1_y8, decoder_416_1_y9, decoder_416_1_y10, decoder_416_1_y11, decoder_416_1_y13);
  or d (Yd, decoder_416_1_y0, decoder_416_1_y2, decoder_416_1_y3, decoder_416_1_y5, decoder_416_1_y6, decoder_416_1_y8, decoder_416_1_y9, decoder_416_1_y11, decoder_416_1_y12, decoder_416_1_y13, decoder_416_1_y14);
  or e (Ye, decoder_416_1_y0, decoder_416_1_y2, decoder_416_1_y6, decoder_416_1_y8, decoder_416_1_y10, decoder_416_1_y11, decoder_416_1_y12, decoder_416_1_y13, decoder_416_1_y14, decoder_416_1_y15);
endmodule

module decoder_24 (
  input  A0,
  input  A1,
  output Y0,
  output Y1,
  output Y2,
  output Y3
);

  wire not_1_out, not_2_out;

  not not_1 (not_1_out, A0);
  not not_2 (not_2_out, A1);
  and and_1 (Y0, not_1_out, not_2_out);
  and and_2 (Y1, A0, not_2_out);
  and and_3 (Y2, not_1_out, A1);
  and and_4 (Y3, A0, A1);
endmodule

module decoder_38 (
  input  A0,
  input  A1,
  input  A2,
  output Y0,
  output Y1,
  output Y2,
  output Y3,
  output Y4,
  output Y5,
  output Y6,
  output Y7
);

  wire decoder_24_1_y0, decoder_24_1_y1, decoder_24_1_y2, decoder_24_1_y3, not_1_out;

  not not_1 (not_1_out, A2);
  decoder_24 decoder_24_1 (
    .A0(A0), .A1(A1), .Y0(decoder_24_1_y0), .Y1(decoder_24_1_y1), .Y2(decoder_24_1_y2), .Y3(decoder_24_1_y3));
  and and_1 (Y0, decoder_24_1_y0, not_1_out);
  and and_2 (Y1, decoder_24_1_y1, not_1_out);
  and and_3 (Y2, decoder_24_1_y2, not_1_out);
  and and_4 (Y3, decoder_24_1_y3, not_1_out);
  and and_5 (Y4, decoder_24_1_y0, A2);
  and and_6 (Y5, decoder_24_1_y1, A2);
  and and_7 (Y6, decoder_24_1_y2, A2);
  and and_8 (Y7, decoder_24_1_y3, A2);
endmodule

module decoder_416 (
  input  A0,
  input  A1,
  input  A2,
  input  A3,
  output Y0,
  output Y1,
  output Y2,
  output Y3,
  output Y4,
  output Y5,
  output Y6,
  output Y7,
  output Y8,
  output Y9,
  output Y10,
  output Y11,
  output Y12,
  output Y13,
  output Y14,
  output Y15
);

  wire decoder_38_1_y0, decoder_38_1_y1, decoder_38_1_y2, decoder_38_1_y3, decoder_38_1_y4, decoder_38_1_y5,
       decoder_38_1_y6, decoder_38_1_y7, not_1_out;

  not not_1 (not_1_out, A3);
  decoder_38 decoder_38_1 (
    .A0(A0), .A1(A1), .A2(A2), .Y0(decoder_38_1_y0), .Y1(decoder_38_1_y1), .Y2(decoder_38_1_y2),
    .Y3(decoder_38_1_y3), .Y4(decoder_38_1_y4), .Y5(decoder_38_1_y5), .Y6(decoder_38_1_y6),
    .Y7(decoder_38_1_y7));
  and and_1 (Y0, decoder_38_1_y0, not_1_out);
  and and_2 (Y1, decoder_38_1_y1, not_1_out);
  and and_3 (Y2, decoder_38_1_y2, not_1_out);
  and and_4 (Y3, decoder_38_1_y3, not_1_out);
  and and_5 (Y4, decoder_38_1_y4, not_1_out);
  and and_6 (Y5, decoder_38_1_y5, not_1_out);
  and and_7 (Y6, decoder_38_1_y6, not_1_out);
  and and_8 (Y7, decoder_38_1_y7, not_1_out);
  and and_9 (Y8, decoder_38_1_y0, A3);
  and and_10 (Y9, decoder_38_1_y1, A3);
  and and_11 (Y10, decoder_38_1_y2, A3);
  and and_12 (Y11, decoder_38_1_y3, A3);
  and and_13 (Y12, decoder_38_1_y4, A3);
  and and_14 (Y13, decoder_38_1_y5, A3);
  and and_15 (Y14, decoder_38_1_y6, A3);
  and and_16 (Y15, decoder_38_1_y7, A3);
endmodule
