// Logisim project Add_2.circ as structural Verilog: 2 circuits, main circuit main
module main (
  input  A,
  input  B,
  input  Cin,
  output Sum,
  output Cout
);

  wire half_add_1_c, half_add_1_s, half_add_2_c;

  half_add half_add_1 (.A(A), .B(B), .S(half_add_1_s), .C(half_add_1_c));
  half_add half_add_2 (.A(half_add_1_s), .B(Cin), .S(Sum), .C(half_add_2_c));
  or or_1 (Cout, half_add_1_c, half_add_2_c);
endmodule

module half_add (
  input  A,
  input  B,
  output S,
  output C
);

  xor xor_1 (S, A, B);
  and and_1 (C, A, B);
endmodule
