// Logisim project D_FlipFlop_aBitFlip.circ as structural Verilog: 5 circuits, main circuit main
module main (
  input  R,
  input  D,
  input  clk,
  output Q
);

  wire d_flipflop_reset_1_q, not_1_out;

  D_FlipFlop_Reset d_flipflop_reset_1 (.D(D), .clk(clk), .Reset(R), .Q(d_flipflop_reset_1_q));
  not not_1 (not_1_out, d_flipflop_reset_1_q);
  D_FlipFlop_Reset d_flipflop_reset_2 (.D(not_1_out), .clk(clk), .Reset(R), .Q(Q));
endmodule

module D_latch_Reset (
  input  WE,
  input  D,
  input  Reset,
  output Q,
  output Q_bar
);

  wire not_1_out, not_2_out, R_out, S_out;

  not not_1 (not_1_out, D);
  not not_2 (not_2_out, Reset);
  and S (S_out, not_1_out, WE);
  and R (R_out, WE, not_2_out, D);
  nor nor_1 (Q, S_out, Reset, Q_bar);
  nor nor_2 (Q_bar, R_out, Q);
endmodule

module D_latch (
  input  WE,
  input  D,
  output Q,
  output Q_bar
);

  wire not_1_out, R_out, S_out;

  not not_1 (not_1_out, D);
  and S (S_out, not_1_out, WE);
  and R (R_out, WE, D);
  nor nor_1 (Q, S_out, Q_bar);
  nor nor_2 (Q_bar, R_out, Q);
endmodule

module D_FlipFlop_Reset (
  input  D,
  input  clk,
  input  Reset,
  output Q
);

  wire d_latch_1_q, not_1_out;

  not not_1 (not_1_out, clk);
  D_latch d_latch_1 (.WE(D), .D(not_1_out), .Q(d_latch_1_q));  // open: Q_bar
  D_latch_Reset d_latch_reset_1 (.WE(d_latch_1_q), .D(clk), .Reset(Reset), .Q(Q));  // open: Q_bar
endmodule

module D_FlipFlop (
  input  D,
  input  clk,
  output Q
);

  wire d_latch_1_q, not_1_out;

  not not_1 (not_1_out, clk);
  D_latch d_latch_1 (.WE(D), .D(not_1_out), .Q(d_latch_1_q));  // open: Q_bar
  D_latch d_latch_2 (.WE(d_latch_1_q), .D(clk), .Q(Q));  // open: Q_bar
endmodule
