// Logisim project D_FlipFlop_neg.circ as structural Verilog: 2 circuits, main circuit main
module main (
  input  D,
  output Q
);

  wire clk_out, d_latch_1_q, not_1_out;

  Button clk (.out(clk_out));
  not not_1 (not_1_out, clk_out);
  D_latch d_latch_1 (.WE(D), .D(clk_out), .Q(d_latch_1_q));  // open: Q_bar
  D_latch d_latch_2 (.WE(d_latch_1_q), .D(not_1_out), .Q(Q));  // open: Q_bar
endmodule

module D_latch (
  input  WE,
  input  D,
  output Q,
  output Q_bar
);

  wire not_1_out, R_out, S_out;

  not not_1 (not_1_out, D);
  and S (S_out, not_1_out, WE);
  and R (R_out, WE, D);
  nor nor_1 (Q, S_out, Q_bar);
  nor nor_2 (Q_bar, R_out, Q);
endmodule
