// Logisim project D_latch_1.circ as structural Verilog: 2 circuits, main circuit main
module main (
  input  WE,
  input  D,
  output Q,
  output Q_bar
);

  wire not_1_out, R_out, S_out;

  not not_1 (not_1_out, D);
  and R (R_out, not_1_out, WE);
  and S (S_out, WE, D);
  SR_latch_NOR sr_latch_nor_1 (.R(R_out), .S(S_out), .Q(Q), .Q_bar(Q_bar));
endmodule

module SR_latch_NOR (
  input  R,
  input  S,
  output Q,
  output Q_bar
);

  nor nor_1 (Q, R, Q_bar);
  nor nor_2 (Q_bar, S, Q);
endmodule
