// Logisim project D_latch_2.circ as structural Verilog: 2 circuits, main circuit main
module main (
  input  D,
  input  WE,
  output Q,
  output Q_bar
);

  wire R_bar_out, S_bar_out;

  nand R_bar (R_bar_out, D, WE);
  nand S_bar (S_bar_out, R_bar_out, WE);
  SR_latch_NAND sr_latch_nand_1 (.R_bar(R_bar_out), .S_bar(S_bar_out), .Q(Q), .Q_bar(Q_bar));
endmodule

module SR_latch_NAND (
  input  R_bar,
  input  S_bar,
  output Q,
  output Q_bar
);

  nand nand_1 (Q, R_bar, Q_bar);
  nand nand_2 (Q_bar, Q, S_bar);
endmodule
