// Logisim project Mux4_3.circ as structural Verilog: 1 circuit, main circuit main
module main (
  input  D00,
  input  S0,
  input  D10,
  input  S1,
  input  D20,
  input  D30,
  input  D01,
  input  D11,
  input  D21,
  input  D31,
  input  D02,
  input  D12,
  input  D22,
  input  D32,
  output Y0,
  output Y1,
  output Y2
);

  wire and_1_out, and_2_out, and_3_out, and_4_out, and_5_out, and_6_out, and_7_out, and_8_out, and_9_out,
       and_10_out, and_11_out, and_12_out, and_13_out, and_14_out, and_15_out, and_16_out, not_1_out,
       not_2_out;

  not not_1 (not_1_out, S0);
  not not_2 (not_2_out, S1);
  and and_1 (and_1_out, not_1_out, not_2_out);
  and and_2 (and_2_out, not_1_out, S1);
  and and_3 (and_3_out, S0, not_2_out);
  and and_4 (and_4_out, S0, S1);
  and and_5 (and_5_out, D00, and_1_out);
  and and_6 (and_6_out, D10, and_2_out);
  and and_7 (and_7_out, D20, and_3_out);
  and and_8 (and_8_out, D30, and_4_out);
  and and_9 (and_9_out, D01, and_1_out);
  and and_10 (and_10_out, D11, and_2_out);
  and and_11 (and_11_out, D21, and_3_out);
  and and_12 (and_12_out, D31, and_4_out);
  and and_13 (and_13_out, D02, and_1_out);
  and and_14 (and_14_out, D12, and_2_out);
  and and_15 (and_15_out, D22, and_3_out);
  and and_16 (and_16_out, D32, and_4_out);
  or or_1 (Y1, and_9_out, and_10_out, and_11_out, and_12_out);
  or or_2 (Y2, and_13_out, and_14_out, and_15_out, and_16_out);
  or or_3 (Y0, and_5_out, and_6_out, and_7_out, and_8_out);
endmodule
