// Logisim project Register_4bit.circ as structural Verilog: 10 circuits, main circuit main
module main (
  input  R,
  input  EN
);

  wire clk_out, dipswitch_1_p1, dipswitch_1_p2, dipswitch_1_p3, dipswitch_1_p4, register4bit_1_q0,
       register4bit_1_q1, register4bit_1_q2, register4bit_1_q3, seg7_h_1_ya, seg7_h_1_yb, seg7_h_1_yc,
       seg7_h_1_yd, seg7_h_1_ye, seg7_h_1_yf, seg7_h_1_yg;

  Button clk (.out(clk_out));
  // DipSwitch #(.number(4)) dipswitch_1: pin names not known; wires that end beside it: dipswitch_1_p1, dipswitch_1_p2, dipswitch_1_p3, dipswitch_1_p4
  register4bit register4bit_1 (
    .R(R), .D0(dipswitch_1_p4), .EN(EN), .clk(clk_out), .D1(dipswitch_1_p3), .D2(dipswitch_1_p2),
    .D3(dipswitch_1_p1), .Q0(register4bit_1_q0), .Q1(register4bit_1_q1), .Q2(register4bit_1_q2),
    .Q3(register4bit_1_q3));  // open: Q0_bar, Q1_bar, Q2_bar, Q3_bar
  Seg7_H seg7_h_1 (
    .A0(register4bit_1_q0), .A1(register4bit_1_q1), .A2(register4bit_1_q2), .A3(register4bit_1_q3),
    .Yg(seg7_h_1_yg), .Yf(seg7_h_1_yf), .Ya(seg7_h_1_ya), .Yb(seg7_h_1_yb), .Yc(seg7_h_1_yc),
    .Yd(seg7_h_1_yd), .Ye(seg7_h_1_ye));
  _7_Segment_Display u_7_segment_display_1 (
    .g(seg7_h_1_yg), .f(seg7_h_1_yf), .a(seg7_h_1_ya), .b(seg7_h_1_yb), .e(seg7_h_1_ye), .d(seg7_h_1_yd),
    .c(seg7_h_1_yc));  // open: dp
endmodule

module Seg7_H (
  input  A0,
  input  A1,
  input  A2,
  input  A3,
  output Yg,
  output Yf,
  output Ya,
  output Yb,
  output Yc,
  output Yd,
  output Ye
);

  wire decoder_416_1_y0, decoder_416_1_y1, decoder_416_1_y2, decoder_416_1_y3, decoder_416_1_y4,
       decoder_416_1_y5, decoder_416_1_y6, decoder_416_1_y7, decoder_416_1_y8, decoder_416_1_y9,
       decoder_416_1_y10, decoder_416_1_y11, decoder_416_1_y12, decoder_416_1_y13, decoder_416_1_y14,
       decoder_416_1_y15;

  decoder_416 decoder_416_1 (
    .A0(A0), .A1(A1), .A2(A2), .A3(A3), .Y0(decoder_416_1_y0), .Y1(decoder_416_1_y1), .Y2(decoder_416_1_y2),
    .Y3(decoder_416_1_y3), .Y4(decoder_416_1_y4), .Y5(decoder_416_1_y5), .Y6(decoder_416_1_y6),
    .Y7(decoder_416_1_y7), .Y8(decoder_416_1_y8), .Y9(decoder_416_1_y9), .Y10(decoder_416_1_y10),
    .Y11(decoder_416_1_y11), .Y12(decoder_416_1_y12), .Y13(decoder_416_1_y13), .Y14(decoder_416_1_y14),
    .Y15(decoder_416_1_y15));
  or g (Yg, decoder_416_1_y2, decoder_416_1_y3, decoder_416_1_y4, decoder_416_1_y5, decoder_416_1_y6, decoder_416_1_y8, decoder_416_1_y9, decoder_416_1_y10, decoder_416_1_y11, decoder_416_1_y13, decoder_416_1_y14, decoder_416_1_y15);
  or f (Yf, decoder_416_1_y0, decoder_416_1_y4, decoder_416_1_y5, decoder_416_1_y6, decoder_416_1_y8, decoder_416_1_y9, decoder_416_1_y10, decoder_416_1_y11, decoder_416_1_y12, decoder_416_1_y14, decoder_416_1_y15);
  or a (Ya, decoder_416_1_y0, decoder_416_1_y2, decoder_416_1_y3, decoder_416_1_y5, decoder_416_1_y6, decoder_416_1_y7, decoder_416_1_y8, decoder_416_1_y9, decoder_416_1_y10, decoder_416_1_y12, decoder_416_1_y14, decoder_416_1_y15);
  or b (Yb, decoder_416_1_y0, decoder_416_1_y1, decoder_416_1_y2, decoder_416_1_y3, decoder_416_1_y4, decoder_416_1_y7, decoder_416_1_y8, decoder_416_1_y9, decoder_416_1_y10, decoder_416_1_y13);
  or c (Yc, decoder_416_1_y0, decoder_416_1_y1, decoder_416_1_y3, decoder_416_1_y4, decoder_416_1_y5, decoder_416_1_y6, decoder_416_1_y7, decoder_416_1_y8, decoder_416_1_y9, decoder_416_1_y10, decoder_416_1_y11, decoder_416_1_y13);
  or d (Yd, decoder_416_1_y0, decoder_416_1_y2, decoder_416_1_y3, decoder_416_1_y5, decoder_416_1_y6, decoder_416_1_y8, decoder_416_1_y9, decoder_416_1_y11, decoder_416_1_y12, decoder_416_1_y13, decoder_416_1_y14);
  or e (Ye, decoder_416_1_y0, decoder_416_1_y2, decoder_416_1_y6, decoder_416_1_y8, decoder_416_1_y10, decoder_416_1_y11, decoder_416_1_y12, decoder_416_1_y13, decoder_416_1_y14, decoder_416_1_y15);
endmodule

module decoder_24 (
  input  A0,
  input  A1,
  output Y0,
  output Y1,
  output Y2,
  output Y3
);

  wire not_1_out, not_2_out;

  not not_1 (not_1_out, A0);
  not not_2 (not_2_out, A1);
  and and_1 (Y0, not_1_out, not_2_out);
  and and_2 (Y1, A0, not_2_out);
  and and_3 (Y2, not_1_out, A1);
  and and_4 (Y3, A0, A1);
endmodule

module decoder_38 (
  input  A0,
  input  A1,
  input  A2,
  output Y0,
  output Y1,
  output Y2,
  output Y3,
  output Y4,
  output Y5,
  output Y6,
  output Y7
);

  wire decoder_24_1_y0, decoder_24_1_y1, decoder_24_1_y2, decoder_24_1_y3, not_1_out;

  not not_1 (not_1_out, A2);
  decoder_24 decoder_24_1 (
    .A0(A0), .A1(A1), .Y0(decoder_24_1_y0), .Y1(decoder_24_1_y1), .Y2(decoder_24_1_y2), .Y3(decoder_24_1_y3));
  and and_1 (Y0, decoder_24_1_y0, not_1_out);
  and and_2 (Y1, decoder_24_1_y1, not_1_out);
  and and_3 (Y2, decoder_24_1_y2, not_1_out);
  and and_4 (Y3, decoder_24_1_y3, not_1_out);
  and and_5 (Y4, decoder_24_1_y0, A2);
  and and_6 (Y5, decoder_24_1_y1, A2);
  and and_7 (Y6, decoder_24_1_y2, A2);
  and and_8 (Y7, decoder_24_1_y3, A2);
endmodule

module decoder_416 (
  input  A0,
  input  A1,
  input  A2,
  input  A3,
  output Y0,
  output Y1,
  output Y2,
  output Y3,
  output Y4,
  output Y5,
  output Y6,
  output Y7,
  output Y8,
  output Y9,
  output Y10,
  output Y11,
  output Y12,
  output Y13,
  output Y14,
  output Y15
);

  wire decoder_38_1_y0, decoder_38_1_y1, decoder_38_1_y2, decoder_38_1_y3, decoder_38_1_y4, decoder_38_1_y5,
       decoder_38_1_y6, decoder_38_1_y7, not_1_out;

  not not_1 (not_1_out, A3);
  decoder_38 decoder_38_1 (
    .A0(A0), .A1(A1), .A2(A2), .Y0(decoder_38_1_y0), .Y1(decoder_38_1_y1), .Y2(decoder_38_1_y2),
    .Y3(decoder_38_1_y3), .Y4(decoder_38_1_y4), .Y5(decoder_38_1_y5), .Y6(decoder_38_1_y6),
    .Y7(decoder_38_1_y7));
  and and_1 (Y0, decoder_38_1_y0, not_1_out);
  and and_2 (Y1, decoder_38_1_y1, not_1_out);
  and and_3 (Y2, decoder_38_1_y2, not_1_out);
  and and_4 (Y3, decoder_38_1_y3, not_1_out);
  and and_5 (Y4, decoder_38_1_y4, not_1_out);
  and and_6 (Y5, decoder_38_1_y5, not_1_out);
  and and_7 (Y6, decoder_38_1_y6, not_1_out);
  and and_8 (Y7, decoder_38_1_y7, not_1_out);
  and and_9 (Y8, decoder_38_1_y0, A3);
  and and_10 (Y9, decoder_38_1_y1, A3);
  and and_11 (Y10, decoder_38_1_y2, A3);
  and and_12 (Y11, decoder_38_1_y3, A3);
  and and_13 (Y12, decoder_38_1_y4, A3);
  and and_14 (Y13, decoder_38_1_y5, A3);
  and and_15 (Y14, decoder_38_1_y6, A3);
  and and_16 (Y15, decoder_38_1_y7, A3);
endmodule

module SR_latch_NOR (
  input  R,
  input  S,
  output Q,
  output Q_bar
);

  nor nor_1 (Q, R, Q_bar);
  nor nor_2 (Q_bar, S, Q);
endmodule

module D_latch (
  input  R,
  input  WE,
  input  D,
  output Q,
  output Q_bar
);

  wire and_1_out, and_2_out, not_1_out, not_2_out, or_1_out;

  not not_1 (not_1_out, R);
  not not_2 (not_2_out, D);
  and and_1 (and_1_out, not_1_out, D, WE);
  and and_2 (and_2_out, WE, not_2_out);
  or or_1 (or_1_out, R, and_2_out);
  SR_latch_NOR sr_latch_nor_1 (.R(or_1_out), .S(and_1_out), .Q(Q), .Q_bar(Q_bar));
endmodule

module DFF (
  input  R,
  input  D,
  input  clk,
  output Q,
  output Q_bar
);

  wire d_latch_1_q, not_1_out;

  not not_1 (not_1_out, clk);
  D_latch d_latch_1 (.R(R), .WE(not_1_out), .D(D), .Q(d_latch_1_q));  // open: Q_bar
  D_latch d_latch_2 (.R(R), .WE(clk), .D(d_latch_1_q), .Q(Q), .Q_bar(Q_bar));
endmodule

module DFF_EN (
  input  R,
  input  D,
  input  clk,
  input  EN,
  output Q,
  output Q_bar
);

  wire multiplexer_1_out;

  Multiplexer multiplexer_1 (.in0(Q), .in1(D), .out(multiplexer_1_out), .sel(EN));
  DFF dff_1 (.R(R), .D(multiplexer_1_out), .clk(clk), .Q(Q), .Q_bar(Q_bar));
endmodule

module register4bit (
  input  R,
  input  D0,
  input  EN,
  input  clk,
  input  D1,
  input  D2,
  input  D3,
  output Q0,
  output Q0_bar,
  output Q1,
  output Q1_bar,
  output Q2,
  output Q2_bar,
  output Q3,
  output Q3_bar
);

  DFF_EN dff_en_1 (.R(R), .D(D0), .clk(clk), .EN(EN), .Q(Q0), .Q_bar(Q0_bar));
  DFF_EN dff_en_2 (.R(R), .D(D1), .clk(clk), .EN(EN), .Q(Q1), .Q_bar(Q1_bar));
  DFF_EN dff_en_3 (.R(R), .D(D2), .clk(clk), .EN(EN), .Q(Q2), .Q_bar(Q2_bar));
  DFF_EN dff_en_4 (.R(R), .D(D3), .clk(clk), .EN(EN), .Q(Q3), .Q_bar(Q3_bar));
endmodule
