// Logisim project SR_NAND.circ as structural Verilog: 1 circuit, main circuit main
module main (
  input  R_bar,
  input  S_bar,
  output Q,
  output Q_bar
);

  nand nand_1 (Q, R_bar, Q_bar);
  nand nand_2 (Q_bar, Q, S_bar);
endmodule
