// Logisim project SR_NOR.circ as structural Verilog: 1 circuit, main circuit main
module main (
  input  R,
  input  S,
  output Q,
  output Q_bar
);

  nor nor_1 (Q, R, Q_bar);
  nor nor_2 (Q_bar, S, Q);
endmodule
