// Logisim project Sub_4.circ as structural Verilog: 7 circuits, main circuit main
module main (
  input  A0,
  input  A1,
  input  A2,
  input  A3,
  input  B0,
  input  B1,
  input  B2,
  input  B3,
  input  Cin,
  output S0,
  output S1,
  output S2,
  output S3,
  output Cout
);

  wire full_subtractor_1_cout, full_subtractor_2_cout, full_subtractor_3_cout, seg7_h_1_ya, seg7_h_1_yb,
       seg7_h_1_yc, seg7_h_1_yd, seg7_h_1_ye, seg7_h_1_yf, seg7_h_1_yg, seg7_h_2_ya, seg7_h_2_yb,
       seg7_h_2_yc, seg7_h_2_yd, seg7_h_2_ye, seg7_h_2_yf, seg7_h_2_yg, seg7_h_3_ya, seg7_h_3_yb,
       seg7_h_3_yc, seg7_h_3_yd, seg7_h_3_ye, seg7_h_3_yf, seg7_h_3_yg;

  Seg7_H seg7_h_1 (
    .A0(A0), .A1(A1), .A2(A2), .A3(A3), .Yg(seg7_h_1_yg), .Yf(seg7_h_1_yf), .Ya(seg7_h_1_ya),
    .Yb(seg7_h_1_yb), .Yc(seg7_h_1_yc), .Yd(seg7_h_1_yd), .Ye(seg7_h_1_ye));
  Seg7_H seg7_h_2 (
    .A0(B0), .A1(B1), .A2(B2), .A3(B3), .Yg(seg7_h_2_yg), .Yf(seg7_h_2_yf), .Ya(seg7_h_2_ya),
    .Yb(seg7_h_2_yb), .Yc(seg7_h_2_yc), .Yd(seg7_h_2_yd), .Ye(seg7_h_2_ye));
  full_subtractor full_subtractor_1 (.A(A0), .B(B0), .Cin(Cin), .D(S0), .Cout(full_subtractor_1_cout));
  full_subtractor full_subtractor_2 (
    .A(A1), .B(B1), .Cin(full_subtractor_1_cout), .D(S1), .Cout(full_subtractor_2_cout));
  full_subtractor full_subtractor_3 (
    .A(A2), .B(B2), .Cin(full_subtractor_2_cout), .D(S2), .Cout(full_subtractor_3_cout));
  full_subtractor full_subtractor_4 (.A(A3), .B(B3), .Cin(full_subtractor_3_cout), .D(S3), .Cout(Cout));
  _7_Segment_Display u_7_segment_display_1 (
    .g(seg7_h_1_yg), .f(seg7_h_1_yf), .a(seg7_h_1_ya), .b(seg7_h_1_yb), .e(seg7_h_1_ye), .d(seg7_h_1_yd),
    .c(seg7_h_1_yc));  // open: dp
  _7_Segment_Display u_7_segment_display_2 (
    .g(seg7_h_2_yg), .f(seg7_h_2_yf), .a(seg7_h_2_ya), .b(seg7_h_2_yb), .e(seg7_h_2_ye), .d(seg7_h_2_yd),
    .c(seg7_h_2_yc));  // open: dp
  LED led_1 (.in(Cout));
  Seg7_H seg7_h_3 (
    .A0(S0), .A1(S1), .A2(S2), .A3(S3), .Yg(seg7_h_3_yg), .Yf(seg7_h_3_yf), .Ya(seg7_h_3_ya),
    .Yb(seg7_h_3_yb), .Yc(seg7_h_3_yc), .Yd(seg7_h_3_yd), .Ye(seg7_h_3_ye));
  _7_Segment_Display u_7_segment_display_3 (
    .g(seg7_h_3_yg), .f(seg7_h_3_yf), .a(seg7_h_3_ya), .b(seg7_h_3_yb), .e(seg7_h_3_ye), .d(seg7_h_3_yd),
    .c(seg7_h_3_yc));  // open: dp
endmodule

module full_subtractor (
  input  A,
  input  B,
  input  Cin,
  output D,
  output Cout
);

  wire half_subtractor_1_cout, half_subtractor_1_d, half_subtractor_2_cout;

  half_subtractor half_subtractor_1 (.A(A), .B(B), .D(half_subtractor_1_d), .Cout(half_subtractor_1_cout));
  half_subtractor half_subtractor_2 (.A(half_subtractor_1_d), .B(Cin), .D(D), .Cout(half_subtractor_2_cout));
  or or_1 (Cout, half_subtractor_2_cout, half_subtractor_1_cout);
endmodule

module half_subtractor (
  input  A,
  input  B,
  output D,
  output Cout
);

  wire not_1_out;

  not not_1 (not_1_out, A);
  xor xor_1 (D, A, B);
  and and_1 (Cout, B, not_1_out);
endmodule

module decoder_24 (
  input  A0,
  input  A1,
  output Y0,
  output Y1,
  output Y2,
  output Y3
);

  wire not_1_out, not_2_out;

  not not_1 (not_1_out, A0);
  not not_2 (not_2_out, A1);
  and and_1 (Y0, not_1_out, not_2_out);
  and and_2 (Y1, A0, not_2_out);
  and and_3 (Y2, not_1_out, A1);
  and and_4 (Y3, A0, A1);
endmodule

module decoder_38 (
  input  A0,
  input  A1,
  input  A2,
  output Y0,
  output Y1,
  output Y2,
  output Y3,
  output Y4,
  output Y5,
  output Y6,
  output Y7
);

  wire decoder_24_1_y0, decoder_24_1_y1, decoder_24_1_y2, decoder_24_1_y3, not_1_out;

  not not_1 (not_1_out, A2);
  decoder_24 decoder_24_1 (
    .A0(A0), .A1(A1), .Y0(decoder_24_1_y0), .Y1(decoder_24_1_y1), .Y2(decoder_24_1_y2), .Y3(decoder_24_1_y3));
  and and_1 (Y0, decoder_24_1_y0, not_1_out);
  and and_2 (Y1, decoder_24_1_y1, not_1_out);
  and and_3 (Y2, decoder_24_1_y2, not_1_out);
  and and_4 (Y3, decoder_24_1_y3, not_1_out);
  and and_5 (Y4, decoder_24_1_y0, A2);
  and and_6 (Y5, decoder_24_1_y1, A2);
  and and_7 (Y6, decoder_24_1_y2, A2);
  and and_8 (Y7, decoder_24_1_y3, A2);
endmodule

module decoder_416 (
  input  A0,
  input  A1,
  input  A2,
  input  A3,
  output Y0,
  output Y1,
  output Y2,
  output Y3,
  output Y4,
  output Y5,
  output Y6,
  output Y7,
  output Y8,
  output Y9,
  output Y10,
  output Y11,
  output Y12,
  output Y13,
  output Y14,
  output Y15
);

  wire decoder_38_1_y0, decoder_38_1_y1, decoder_38_1_y2, decoder_38_1_y3, decoder_38_1_y4, decoder_38_1_y5,
       decoder_38_1_y6, decoder_38_1_y7, not_1_out;

  not not_1 (not_1_out, A3);
  decoder_38 decoder_38_1 (
    .A0(A0), .A1(A1), .A2(A2), .Y0(decoder_38_1_y0), .Y1(decoder_38_1_y1), .Y2(decoder_38_1_y2),
    .Y3(decoder_38_1_y3), .Y4(decoder_38_1_y4), .Y5(decoder_38_1_y5), .Y6(decoder_38_1_y6),
    .Y7(decoder_38_1_y7));
  and and_1 (Y0, decoder_38_1_y0, not_1_out);
  and and_2 (Y1, decoder_38_1_y1, not_1_out);
  and and_3 (Y2, decoder_38_1_y2, not_1_out);
  and and_4 (Y3, decoder_38_1_y3, not_1_out);
  and and_5 (Y4, decoder_38_1_y4, not_1_out);
  and and_6 (Y5, decoder_38_1_y5, not_1_out);
  and and_7 (Y6, decoder_38_1_y6, not_1_out);
  and and_8 (Y7, decoder_38_1_y7, not_1_out);
  and and_9 (Y8, decoder_38_1_y0, A3);
  and and_10 (Y9, decoder_38_1_y1, A3);
  and and_11 (Y10, decoder_38_1_y2, A3);
  and and_12 (Y11, decoder_38_1_y3, A3);
  and and_13 (Y12, decoder_38_1_y4, A3);
  and and_14 (Y13, decoder_38_1_y5, A3);
  and and_15 (Y14, decoder_38_1_y6, A3);
  and and_16 (Y15, decoder_38_1_y7, A3);
endmodule

module Seg7_H (
  input  A0,
  input  A1,
  input  A2,
  input  A3,
  output Yg,
  output Yf,
  output Ya,
  output Yb,
  output Yc,
  output Yd,
  output Ye
);

  wire decoder_416_1_y0, decoder_416_1_y1, decoder_416_1_y2, decoder_416_1_y3, decoder_416_1_y4,
       decoder_416_1_y5, decoder_416_1_y6, decoder_416_1_y7, decoder_416_1_y8, decoder_416_1_y9,
       decoder_416_1_y10, decoder_416_1_y11, decoder_416_1_y12, decoder_416_1_y13, decoder_416_1_y14,
       decoder_416_1_y15;

  decoder_416 decoder_416_1 (
    .A0(A0), .A1(A1), .A2(A2), .A3(A3), .Y0(decoder_416_1_y0), .Y1(decoder_416_1_y1), .Y2(decoder_416_1_y2),
    .Y3(decoder_416_1_y3), .Y4(decoder_416_1_y4), .Y5(decoder_416_1_y5), .Y6(decoder_416_1_y6),
    .Y7(decoder_416_1_y7), .Y8(decoder_416_1_y8), .Y9(decoder_416_1_y9), .Y10(decoder_416_1_y10),
    .Y11(decoder_416_1_y11), .Y12(decoder_416_1_y12), .Y13(decoder_416_1_y13), .Y14(decoder_416_1_y14),
    .Y15(decoder_416_1_y15));
  or g (Yg, decoder_416_1_y2, decoder_416_1_y3, decoder_416_1_y4, decoder_416_1_y5, decoder_416_1_y6, decoder_416_1_y8, decoder_416_1_y9, decoder_416_1_y10, decoder_416_1_y11, decoder_416_1_y13, decoder_416_1_y14, decoder_416_1_y15);
  or f (Yf, decoder_416_1_y0, decoder_416_1_y4, decoder_416_1_y5, decoder_416_1_y6, decoder_416_1_y8, decoder_416_1_y9, decoder_416_1_y10, decoder_416_1_y11, decoder_416_1_y12, decoder_416_1_y14, decoder_416_1_y15);
  or a (Ya, decoder_416_1_y0, decoder_416_1_y2, decoder_416_1_y3, decoder_416_1_y5, decoder_416_1_y6, decoder_416_1_y7, decoder_416_1_y8, decoder_416_1_y9, decoder_416_1_y10, decoder_416_1_y12, decoder_416_1_y14, decoder_416_1_y15);
  or b (Yb, decoder_416_1_y0, decoder_416_1_y1, decoder_416_1_y2, decoder_416_1_y3, decoder_416_1_y4, decoder_416_1_y7, decoder_416_1_y8, decoder_416_1_y9, decoder_416_1_y10, decoder_416_1_y13);
  or c (Yc, decoder_416_1_y0, decoder_416_1_y1, decoder_416_1_y3, decoder_416_1_y4, decoder_416_1_y5, decoder_416_1_y6, decoder_416_1_y7, decoder_416_1_y8, decoder_416_1_y9, decoder_416_1_y10, decoder_416_1_y11, decoder_416_1_y13);
  or d (Yd, decoder_416_1_y0, decoder_416_1_y2, decoder_416_1_y3, decoder_416_1_y5, decoder_416_1_y6, decoder_416_1_y8, decoder_416_1_y9, decoder_416_1_y11, decoder_416_1_y12, decoder_416_1_y13, decoder_416_1_y14);
  or e (Ye, decoder_416_1_y0, decoder_416_1_y2, decoder_416_1_y6, decoder_416_1_y8, decoder_416_1_y10, decoder_416_1_y11, decoder_416_1_y12, decoder_416_1_y13, decoder_416_1_y14, decoder_416_1_y15);
endmodule
