// Logisim project XNOR_test02.circ as structural Verilog: 1 circuit, main circuit main
module main (
  input  A,
  input  B,
  output Y
);

  wire transistor_1_out;

  Transistor transistor_1 (.in(1'b1), .out(transistor_1_out), .gate(A));
  Transistor #(.\type ("n")) transistor_2 (.in(1'b0), .out(transistor_1_out), .gate(A));
  Transistor transistor_3 (.in(transistor_1_out), .out(Y), .gate(B));
  Transistor #(.\type ("n")) transistor_4 (.in(A), .out(Y), .gate(B));
  // Transmission_Gate transmission_1: pin names not known; wires that end beside it: Y, transistor_1_out, A, B
endmodule
