// Logisim project cmp.circ as structural Verilog: 1 circuit, main circuit main
module main (
);

  wire A_p1, A_p2, A_p3, A_p4, and_1_out, B_p1, B_p2, B_p3, B_p4, xnor_1_out, xnor_2_out, xnor_3_out,
       xnor_4_out;

  // DipSwitch #(.number(4)) A: pin names not known; wires that end beside it: A_p1, A_p2, A_p3, A_p4
  // DipSwitch #(.number(4)) B: pin names not known; wires that end beside it: B_p1, B_p2, B_p3, B_p4
  xnor xnor_1 (xnor_1_out, A_p1, B_p1);
  xnor xnor_2 (xnor_2_out, A_p2, B_p2);
  xnor xnor_3 (xnor_3_out, A_p3, B_p3);
  xnor xnor_4 (xnor_4_out, A_p4, B_p4);
  and and_1 (and_1_out, xnor_1_out, xnor_2_out, xnor_3_out, xnor_4_out);
  LED led_1 (.in(and_1_out));
endmodule
