// Logisim project full_subtractor.circ as structural Verilog: 2 circuits, main circuit main
module main (
  input  A,
  input  B,
  input  Cin,
  output D,
  output Cout
);

  wire half_subtractor_1_cout, half_subtractor_1_d, half_subtractor_2_cout;

  half_subtractor half_subtractor_1 (.A(A), .B(B), .D(half_subtractor_1_d), .Cout(half_subtractor_1_cout));
  half_subtractor half_subtractor_2 (.A(half_subtractor_1_d), .B(Cin), .D(D), .Cout(half_subtractor_2_cout));
  or or_1 (Cout, half_subtractor_2_cout, half_subtractor_1_cout);
endmodule

module half_subtractor (
  input  A,
  input  B,
  output D,
  output Cout
);

  wire not_1_out;

  not not_1 (not_1_out, A);
  xor xor_1 (D, A, B);
  and and_1 (Cout, B, not_1_out);
endmodule
