// Logisim project half_subtractor.circ as structural Verilog: 1 circuit, main circuit main
module main (
  input  A,
  input  B,
  output D,
  output Cout
);

  wire not_1_out;

  not not_1 (not_1_out, A);
  xor xor_1 (D, A, B);
  and and_1 (Cout, B, not_1_out);
endmodule
