// Logisim project ones_complement_adder.circ as structural Verilog: 16 circuits, main circuit main
module main (
  input  B3,
  input  B2,
  input  B1,
  input  B0,
  input  A3,
  input  A2,
  input  A1,
  input  A0,
  output Y0,
  output Y1,
  output Y2,
  output Y3
);

  wire add_4_1_s0, add_4_1_s1, add_4_1_s2, and_1_out, and_2_out, mux_3bit_4to1_1_y0, mux_3bit_4to1_1_y1,
       mux_3bit_4to1_1_y2, mux_4bit_2to1_1_y0, mux_4bit_2to1_1_y1, mux_4bit_2to1_1_y2, mux_4bit_2to1_1_y3,
       mux_4bit_2to1_2_y0, mux_4bit_2to1_2_y1, mux_4bit_2to1_2_y2, mux_4bit_2to1_2_y3, not_1_out, not_2_out,
       not_3_out, not_4_out, not_5_out, not_6_out, not_7_out, seg7_o_1_ya, seg7_o_1_yb, seg7_o_1_yc,
       seg7_o_1_yd, seg7_o_1_ye, seg7_o_1_yf, seg7_o_1_yg, sub_4_1_cout, sub_4_1_s0, sub_4_1_s1, sub_4_1_s2,
       sub_4_2_s0, sub_4_2_s1, sub_4_2_s2, xor_1_out;

  and and_1 (and_1_out, 1'b1, B3);
  not not_1 (not_1_out, B2);
  not not_2 (not_2_out, B1);
  Mux_4bit_2to1 mux_4bit_2to1_1 (
    .D00(B0), .D10(not_3_out), .D01(B1), .S(and_1_out), .D11(not_2_out), .D02(B2), .D12(not_1_out), .D03(B3),
    .D13(B3), .Y0(mux_4bit_2to1_1_y0), .Y1(mux_4bit_2to1_1_y1), .Y2(mux_4bit_2to1_1_y2),
    .Y3(mux_4bit_2to1_1_y3));
  not not_3 (not_3_out, B0);
  and and_2 (and_2_out, 1'b1, A3);
  not not_4 (not_4_out, A2);
  not not_5 (not_5_out, A1);
  Mux_4bit_2to1 mux_4bit_2to1_2 (
    .D00(A0), .D10(not_6_out), .D01(A1), .S(and_2_out), .D11(not_5_out), .D02(A2), .D12(not_4_out), .D03(A3),
    .D13(A3), .Y0(mux_4bit_2to1_2_y0), .Y1(mux_4bit_2to1_2_y1), .Y2(mux_4bit_2to1_2_y2),
    .Y3(mux_4bit_2to1_2_y3));
  not not_6 (not_6_out, A0);
  xor xor_1 (xor_1_out, mux_4bit_2to1_2_y3, mux_4bit_2to1_1_y3);
  not not_7 (not_7_out, xor_1_out);
  Add_4 add_4_1 (
    .A0(mux_4bit_2to1_2_y0), .A1(mux_4bit_2to1_2_y1), .A2(mux_4bit_2to1_2_y2), .A3(1'b0),
    .B0(mux_4bit_2to1_1_y0), .B1(mux_4bit_2to1_1_y1), .B2(mux_4bit_2to1_1_y2), .B3(1'b0), .Cin(1'b0),
    .S0(add_4_1_s0), .S1(add_4_1_s1), .S2(add_4_1_s2));  // open: S3, C4
  Sub_4 sub_4_1 (
    .A0(mux_4bit_2to1_2_y0), .A1(mux_4bit_2to1_2_y1), .A2(mux_4bit_2to1_2_y2), .A3(1'b0),
    .B0(mux_4bit_2to1_1_y0), .B1(mux_4bit_2to1_1_y1), .B2(mux_4bit_2to1_1_y2), .B3(1'b0), .Cin(1'b0),
    .S0(sub_4_1_s0), .S1(sub_4_1_s1), .S2(sub_4_1_s2), .Cout(sub_4_1_cout));  // open: S3
  Sub_4 sub_4_2 (
    .A0(mux_4bit_2to1_1_y0), .A1(mux_4bit_2to1_1_y1), .A2(mux_4bit_2to1_1_y2), .A3(1'b0),
    .B0(mux_4bit_2to1_2_y0), .B1(mux_4bit_2to1_2_y1), .B2(mux_4bit_2to1_2_y2), .B3(1'b0), .Cin(1'b0),
    .S0(sub_4_2_s0), .S1(sub_4_2_s1), .S2(sub_4_2_s2));  // open: S3, Cout
  Mux_3bit_4to1 mux_3bit_4to1_1 (
    .D00(sub_4_1_s0), .S1(not_7_out), .D10(sub_4_2_s0), .S0(sub_4_1_cout), .D20(add_4_1_s0),
    .D30(add_4_1_s0), .D01(sub_4_1_s1), .D11(sub_4_2_s1), .D21(add_4_1_s1), .D31(add_4_1_s1),
    .D02(sub_4_1_s2), .D12(sub_4_2_s2), .D22(add_4_1_s2), .D32(add_4_1_s2), .Y0(mux_3bit_4to1_1_y0),
    .Y1(mux_3bit_4to1_1_y1), .Y2(mux_3bit_4to1_1_y2));
  Mux_1bit_4to1 mux_1bit_4to1_1 (
    .D0(mux_4bit_2to1_2_y3), .S1(not_7_out), .S0(sub_4_1_cout), .D1(mux_4bit_2to1_1_y3),
    .D2(mux_4bit_2to1_1_y3), .D3(mux_4bit_2to1_2_y3), .Y(Y3));
  xor xor_2 (Y0, mux_3bit_4to1_1_y0, Y3);
  xor xor_3 (Y1, mux_3bit_4to1_1_y1, Y3);
  xor xor_4 (Y2, mux_3bit_4to1_1_y2, Y3);
  Seg7_O seg7_o_1 (
    .A0(mux_3bit_4to1_1_y0), .A1(mux_3bit_4to1_1_y1), .A2(mux_3bit_4to1_1_y2), .A3(1'b0), .Yg(seg7_o_1_yg),
    .Yf(seg7_o_1_yf), .Ya(seg7_o_1_ya), .Yb(seg7_o_1_yb), .Yc(seg7_o_1_yc), .Yd(seg7_o_1_yd), .Ye(seg7_o_1_ye));  // open: Yother
  _7_Segment_Display u_7_segment_display_1 (.g(Y3));  // open: f, a, b, e, d, c, dp
  _7_Segment_Display u_7_segment_display_2 (
    .g(seg7_o_1_yg), .f(seg7_o_1_yf), .a(seg7_o_1_ya), .b(seg7_o_1_yb), .e(seg7_o_1_ye), .d(seg7_o_1_yd),
    .c(seg7_o_1_yc));  // open: dp
endmodule

module Add_4 (
  input  A0,
  input  A1,
  input  A2,
  input  A3,
  input  B0,
  input  B1,
  input  B2,
  input  B3,
  input  Cin,
  output S0,
  output S1,
  output S2,
  output S3,
  output C4
);

  wire add_2_1_cout, add_2_2_cout, add_2_3_cout, seg7_h_1_ya, seg7_h_1_yb, seg7_h_1_yc, seg7_h_1_yd,
       seg7_h_1_ye, seg7_h_1_yf, seg7_h_1_yg, seg7_h_2_ya, seg7_h_2_yb, seg7_h_2_yc, seg7_h_2_yd,
       seg7_h_2_ye, seg7_h_2_yf, seg7_h_2_yg, seg7_h_3_ya, seg7_h_3_yb, seg7_h_3_yc, seg7_h_3_yd,
       seg7_h_3_ye, seg7_h_3_yf, seg7_h_3_yg;

  Seg7_H seg7_h_1 (
    .A0(A0), .A1(A1), .A2(A2), .A3(A3), .Yg(seg7_h_1_yg), .Yf(seg7_h_1_yf), .Ya(seg7_h_1_ya),
    .Yb(seg7_h_1_yb), .Yc(seg7_h_1_yc), .Yd(seg7_h_1_yd), .Ye(seg7_h_1_ye));
  Seg7_H seg7_h_2 (
    .A0(B0), .A1(B1), .A2(B2), .A3(B3), .Yg(seg7_h_2_yg), .Yf(seg7_h_2_yf), .Ya(seg7_h_2_ya),
    .Yb(seg7_h_2_yb), .Yc(seg7_h_2_yc), .Yd(seg7_h_2_yd), .Ye(seg7_h_2_ye));
  Add_2 add_2_1 (.A(A0), .B(B0), .Cin(Cin), .Sum(S0), .Cout(add_2_1_cout));
  Add_2 add_2_2 (.A(A1), .B(B1), .Cin(add_2_1_cout), .Sum(S1), .Cout(add_2_2_cout));
  Add_2 add_2_3 (.A(A2), .B(B2), .Cin(add_2_2_cout), .Sum(S2), .Cout(add_2_3_cout));
  Add_2 add_2_4 (.A(A3), .B(B3), .Cin(add_2_3_cout), .Sum(S3), .Cout(C4));
  _7_Segment_Display u_7_segment_display_1 (
    .g(seg7_h_1_yg), .f(seg7_h_1_yf), .a(seg7_h_1_ya), .b(seg7_h_1_yb), .e(seg7_h_1_ye), .d(seg7_h_1_yd),
    .c(seg7_h_1_yc));  // open: dp
  _7_Segment_Display u_7_segment_display_2 (
    .g(seg7_h_2_yg), .f(seg7_h_2_yf), .a(seg7_h_2_ya), .b(seg7_h_2_yb), .e(seg7_h_2_ye), .d(seg7_h_2_yd),
    .c(seg7_h_2_yc));  // open: dp
  LED led_1 (.in(C4));
  Seg7_H seg7_h_3 (
    .A0(S0), .A1(S1), .A2(S2), .A3(S3), .Yg(seg7_h_3_yg), .Yf(seg7_h_3_yf), .Ya(seg7_h_3_ya),
    .Yb(seg7_h_3_yb), .Yc(seg7_h_3_yc), .Yd(seg7_h_3_yd), .Ye(seg7_h_3_ye));
  _7_Segment_Display u_7_segment_display_3 (
    .g(seg7_h_3_yg), .f(seg7_h_3_yf), .a(seg7_h_3_ya), .b(seg7_h_3_yb), .e(seg7_h_3_ye), .d(seg7_h_3_yd),
    .c(seg7_h_3_yc));  // open: dp
endmodule

module Add_2 (
  input  A,
  input  B,
  input  Cin,
  output Sum,
  output Cout
);

  wire half_add_1_c, half_add_1_s, half_add_2_c;

  half_add half_add_1 (.A(A), .B(B), .S(half_add_1_s), .C(half_add_1_c));
  half_add half_add_2 (.A(half_add_1_s), .B(Cin), .S(Sum), .C(half_add_2_c));
  or or_1 (Cout, half_add_1_c, half_add_2_c);
endmodule

module half_add (
  input  A,
  input  B,
  output S,
  output C
);

  xor xor_1 (S, A, B);
  and and_1 (C, A, B);
endmodule

module Seg7_H (
  input  A0,
  input  A1,
  input  A2,
  input  A3,
  output Yg,
  output Yf,
  output Ya,
  output Yb,
  output Yc,
  output Yd,
  output Ye
);

  wire decoder_416_1_y0, decoder_416_1_y1, decoder_416_1_y2, decoder_416_1_y3, decoder_416_1_y4,
       decoder_416_1_y5, decoder_416_1_y6, decoder_416_1_y7, decoder_416_1_y8, decoder_416_1_y9,
       decoder_416_1_y10, decoder_416_1_y11, decoder_416_1_y12, decoder_416_1_y13, decoder_416_1_y14,
       decoder_416_1_y15;

  decoder_416 decoder_416_1 (
    .A0(A0), .A1(A1), .A2(A2), .A3(A3), .Y0(decoder_416_1_y0), .Y1(decoder_416_1_y1), .Y2(decoder_416_1_y2),
    .Y3(decoder_416_1_y3), .Y4(decoder_416_1_y4), .Y5(decoder_416_1_y5), .Y6(decoder_416_1_y6),
    .Y7(decoder_416_1_y7), .Y8(decoder_416_1_y8), .Y9(decoder_416_1_y9), .Y10(decoder_416_1_y10),
    .Y11(decoder_416_1_y11), .Y12(decoder_416_1_y12), .Y13(decoder_416_1_y13), .Y14(decoder_416_1_y14),
    .Y15(decoder_416_1_y15));
  or g (Yg, decoder_416_1_y2, decoder_416_1_y3, decoder_416_1_y4, decoder_416_1_y5, decoder_416_1_y6, decoder_416_1_y8, decoder_416_1_y9, decoder_416_1_y10, decoder_416_1_y11, decoder_416_1_y13, decoder_416_1_y14, decoder_416_1_y15);
  or f (Yf, decoder_416_1_y0, decoder_416_1_y4, decoder_416_1_y5, decoder_416_1_y6, decoder_416_1_y8, decoder_416_1_y9, decoder_416_1_y10, decoder_416_1_y11, decoder_416_1_y12, decoder_416_1_y14, decoder_416_1_y15);
  or a (Ya, decoder_416_1_y0, decoder_416_1_y2, decoder_416_1_y3, decoder_416_1_y5, decoder_416_1_y6, decoder_416_1_y7, decoder_416_1_y8, decoder_416_1_y9, decoder_416_1_y10, decoder_416_1_y12, decoder_416_1_y14, decoder_416_1_y15);
  or b (Yb, decoder_416_1_y0, decoder_416_1_y1, decoder_416_1_y2, decoder_416_1_y3, decoder_416_1_y4, decoder_416_1_y7, decoder_416_1_y8, decoder_416_1_y9, decoder_416_1_y10, decoder_416_1_y13);
  or c (Yc, decoder_416_1_y0, decoder_416_1_y1, decoder_416_1_y3, decoder_416_1_y4, decoder_416_1_y5, decoder_416_1_y6, decoder_416_1_y7, decoder_416_1_y8, decoder_416_1_y9, decoder_416_1_y10, decoder_416_1_y11, decoder_416_1_y13);
  or d (Yd, decoder_416_1_y0, decoder_416_1_y2, decoder_416_1_y3, decoder_416_1_y5, decoder_416_1_y6, decoder_416_1_y8, decoder_416_1_y9, decoder_416_1_y11, decoder_416_1_y12, decoder_416_1_y13, decoder_416_1_y14);
  or e (Ye, decoder_416_1_y0, decoder_416_1_y2, decoder_416_1_y6, decoder_416_1_y8, decoder_416_1_y10, decoder_416_1_y11, decoder_416_1_y12, decoder_416_1_y13, decoder_416_1_y14, decoder_416_1_y15);
endmodule

module Seg7_O (
  input  A0,
  input  A1,
  input  A2,
  input  A3,
  output Yg,
  output Yf,
  output Ya,
  output Yb,
  output Yc,
  output Yd,
  output Ye,
  output Yother
);

  wire decoder_416_1_y0, decoder_416_1_y1, decoder_416_1_y2, decoder_416_1_y3, decoder_416_1_y4,
       decoder_416_1_y5, decoder_416_1_y6, decoder_416_1_y7, decoder_416_1_y8, decoder_416_1_y9,
       decoder_416_1_y10, decoder_416_1_y11, decoder_416_1_y12, decoder_416_1_y13, decoder_416_1_y14,
       decoder_416_1_y15;

  decoder_416 decoder_416_1 (
    .A0(A0), .A1(A1), .A2(A2), .A3(A3), .Y0(decoder_416_1_y0), .Y1(decoder_416_1_y1), .Y2(decoder_416_1_y2),
    .Y3(decoder_416_1_y3), .Y4(decoder_416_1_y4), .Y5(decoder_416_1_y5), .Y6(decoder_416_1_y6),
    .Y7(decoder_416_1_y7), .Y8(decoder_416_1_y8), .Y9(decoder_416_1_y9), .Y10(decoder_416_1_y10),
    .Y11(decoder_416_1_y11), .Y12(decoder_416_1_y12), .Y13(decoder_416_1_y13), .Y14(decoder_416_1_y14),
    .Y15(decoder_416_1_y15));
  or g (Yg, decoder_416_1_y2, decoder_416_1_y3, decoder_416_1_y4, decoder_416_1_y5, decoder_416_1_y6, decoder_416_1_y8, decoder_416_1_y9);
  or f (Yf, decoder_416_1_y0, decoder_416_1_y4, decoder_416_1_y5, decoder_416_1_y6, decoder_416_1_y8, decoder_416_1_y9);
  or a (Ya, decoder_416_1_y0, decoder_416_1_y2, decoder_416_1_y3, decoder_416_1_y5, decoder_416_1_y6, decoder_416_1_y7, decoder_416_1_y8, decoder_416_1_y9);
  or b (Yb, decoder_416_1_y0, decoder_416_1_y1, decoder_416_1_y2, decoder_416_1_y3, decoder_416_1_y4, decoder_416_1_y7, decoder_416_1_y8, decoder_416_1_y9);
  or c (Yc, decoder_416_1_y0, decoder_416_1_y1, decoder_416_1_y3, decoder_416_1_y4, decoder_416_1_y5, decoder_416_1_y6, decoder_416_1_y7, decoder_416_1_y8, decoder_416_1_y9);
  or d (Yd, decoder_416_1_y0, decoder_416_1_y2, decoder_416_1_y3, decoder_416_1_y5, decoder_416_1_y6, decoder_416_1_y8, decoder_416_1_y9);
  or e (Ye, decoder_416_1_y0, decoder_416_1_y2, decoder_416_1_y6, decoder_416_1_y8);
  or other (Yother, decoder_416_1_y10, decoder_416_1_y11, decoder_416_1_y12, decoder_416_1_y13, decoder_416_1_y14, decoder_416_1_y15);
endmodule

module decoder_24 (
  input  A0,
  input  A1,
  output Y0,
  output Y1,
  output Y2,
  output Y3
);

  wire not_1_out, not_2_out;

  not not_1 (not_1_out, A0);
  not not_2 (not_2_out, A1);
  and and_1 (Y0, not_1_out, not_2_out);
  and and_2 (Y1, A0, not_2_out);
  and and_3 (Y2, not_1_out, A1);
  and and_4 (Y3, A0, A1);
endmodule

module decoder_38 (
  input  A0,
  input  A1,
  input  A2,
  output Y0,
  output Y1,
  output Y2,
  output Y3,
  output Y4,
  output Y5,
  output Y6,
  output Y7
);

  wire decoder_24_1_y0, decoder_24_1_y1, decoder_24_1_y2, decoder_24_1_y3, not_1_out;

  not not_1 (not_1_out, A2);
  decoder_24 decoder_24_1 (
    .A0(A0), .A1(A1), .Y0(decoder_24_1_y0), .Y1(decoder_24_1_y1), .Y2(decoder_24_1_y2), .Y3(decoder_24_1_y3));
  and and_1 (Y0, decoder_24_1_y0, not_1_out);
  and and_2 (Y1, decoder_24_1_y1, not_1_out);
  and and_3 (Y2, decoder_24_1_y2, not_1_out);
  and and_4 (Y3, decoder_24_1_y3, not_1_out);
  and and_5 (Y4, decoder_24_1_y0, A2);
  and and_6 (Y5, decoder_24_1_y1, A2);
  and and_7 (Y6, decoder_24_1_y2, A2);
  and and_8 (Y7, decoder_24_1_y3, A2);
endmodule

module decoder_416 (
  input  A0,
  input  A1,
  input  A2,
  input  A3,
  output Y0,
  output Y1,
  output Y2,
  output Y3,
  output Y4,
  output Y5,
  output Y6,
  output Y7,
  output Y8,
  output Y9,
  output Y10,
  output Y11,
  output Y12,
  output Y13,
  output Y14,
  output Y15
);

  wire decoder_38_1_y0, decoder_38_1_y1, decoder_38_1_y2, decoder_38_1_y3, decoder_38_1_y4, decoder_38_1_y5,
       decoder_38_1_y6, decoder_38_1_y7, not_1_out;

  not not_1 (not_1_out, A3);
  decoder_38 decoder_38_1 (
    .A0(A0), .A1(A1), .A2(A2), .Y0(decoder_38_1_y0), .Y1(decoder_38_1_y1), .Y2(decoder_38_1_y2),
    .Y3(decoder_38_1_y3), .Y4(decoder_38_1_y4), .Y5(decoder_38_1_y5), .Y6(decoder_38_1_y6),
    .Y7(decoder_38_1_y7));
  and and_1 (Y0, decoder_38_1_y0, not_1_out);
  and and_2 (Y1, decoder_38_1_y1, not_1_out);
  and and_3 (Y2, decoder_38_1_y2, not_1_out);
  and and_4 (Y3, decoder_38_1_y3, not_1_out);
  and and_5 (Y4, decoder_38_1_y4, not_1_out);
  and and_6 (Y5, decoder_38_1_y5, not_1_out);
  and and_7 (Y6, decoder_38_1_y6, not_1_out);
  and and_8 (Y7, decoder_38_1_y7, not_1_out);
  and and_9 (Y8, decoder_38_1_y0, A3);
  and and_10 (Y9, decoder_38_1_y1, A3);
  and and_11 (Y10, decoder_38_1_y2, A3);
  and and_12 (Y11, decoder_38_1_y3, A3);
  and and_13 (Y12, decoder_38_1_y4, A3);
  and and_14 (Y13, decoder_38_1_y5, A3);
  and and_15 (Y14, decoder_38_1_y6, A3);
  and and_16 (Y15, decoder_38_1_y7, A3);
endmodule

module Sub_4 (
  input  A0,
  input  A1,
  input  A2,
  input  A3,
  input  B0,
  input  B1,
  input  B2,
  input  B3,
  input  Cin,
  output S0,
  output S1,
  output S2,
  output S3,
  output Cout
);

  wire full_subtractor_1_cout, full_subtractor_2_cout, full_subtractor_3_cout, seg7_h_1_ya, seg7_h_1_yb,
       seg7_h_1_yc, seg7_h_1_yd, seg7_h_1_ye, seg7_h_1_yf, seg7_h_1_yg, seg7_h_2_ya, seg7_h_2_yb,
       seg7_h_2_yc, seg7_h_2_yd, seg7_h_2_ye, seg7_h_2_yf, seg7_h_2_yg, seg7_h_3_ya, seg7_h_3_yb,
       seg7_h_3_yc, seg7_h_3_yd, seg7_h_3_ye, seg7_h_3_yf, seg7_h_3_yg;

  Seg7_H seg7_h_1 (
    .A0(A0), .A1(A1), .A2(A2), .A3(A3), .Yg(seg7_h_1_yg), .Yf(seg7_h_1_yf), .Ya(seg7_h_1_ya),
    .Yb(seg7_h_1_yb), .Yc(seg7_h_1_yc), .Yd(seg7_h_1_yd), .Ye(seg7_h_1_ye));
  Seg7_H seg7_h_2 (
    .A0(B0), .A1(B1), .A2(B2), .A3(B3), .Yg(seg7_h_2_yg), .Yf(seg7_h_2_yf), .Ya(seg7_h_2_ya),
    .Yb(seg7_h_2_yb), .Yc(seg7_h_2_yc), .Yd(seg7_h_2_yd), .Ye(seg7_h_2_ye));
  full_subtractor full_subtractor_1 (.A(A0), .B(B0), .Cin(Cin), .D(S0), .Cout(full_subtractor_1_cout));
  full_subtractor full_subtractor_2 (
    .A(A1), .B(B1), .Cin(full_subtractor_1_cout), .D(S1), .Cout(full_subtractor_2_cout));
  full_subtractor full_subtractor_3 (
    .A(A2), .B(B2), .Cin(full_subtractor_2_cout), .D(S2), .Cout(full_subtractor_3_cout));
  full_subtractor full_subtractor_4 (.A(A3), .B(B3), .Cin(full_subtractor_3_cout), .D(S3), .Cout(Cout));
  _7_Segment_Display u_7_segment_display_1 (
    .g(seg7_h_1_yg), .f(seg7_h_1_yf), .a(seg7_h_1_ya), .b(seg7_h_1_yb), .e(seg7_h_1_ye), .d(seg7_h_1_yd),
    .c(seg7_h_1_yc));  // open: dp
  _7_Segment_Display u_7_segment_display_2 (
    .g(seg7_h_2_yg), .f(seg7_h_2_yf), .a(seg7_h_2_ya), .b(seg7_h_2_yb), .e(seg7_h_2_ye), .d(seg7_h_2_yd),
    .c(seg7_h_2_yc));  // open: dp
  LED led_1 (.in(Cout));
  Seg7_H seg7_h_3 (
    .A0(S0), .A1(S1), .A2(S2), .A3(S3), .Yg(seg7_h_3_yg), .Yf(seg7_h_3_yf), .Ya(seg7_h_3_ya),
    .Yb(seg7_h_3_yb), .Yc(seg7_h_3_yc), .Yd(seg7_h_3_yd), .Ye(seg7_h_3_ye));
  _7_Segment_Display u_7_segment_display_3 (
    .g(seg7_h_3_yg), .f(seg7_h_3_yf), .a(seg7_h_3_ya), .b(seg7_h_3_yb), .e(seg7_h_3_ye), .d(seg7_h_3_yd),
    .c(seg7_h_3_yc));  // open: dp
endmodule

module full_subtractor (
  input  A,
  input  B,
  input  Cin,
  output D,
  output Cout
);

  wire half_subtractor_1_cout, half_subtractor_1_d, half_subtractor_2_cout;

  half_subtractor half_subtractor_1 (.A(A), .B(B), .D(half_subtractor_1_d), .Cout(half_subtractor_1_cout));
  half_subtractor half_subtractor_2 (.A(half_subtractor_1_d), .B(Cin), .D(D), .Cout(half_subtractor_2_cout));
  or or_1 (Cout, half_subtractor_2_cout, half_subtractor_1_cout);
endmodule

module half_subtractor (
  input  A,
  input  B,
  output D,
  output Cout
);

  wire not_1_out;

  not not_1 (not_1_out, A);
  xor xor_1 (D, A, B);
  and and_1 (Cout, B, not_1_out);
endmodule

module Mux_3bit_4to1 (
  input  D00,
  input  S1,
  input  D10,
  input  S0,
  input  D20,
  input  D30,
  input  D01,
  input  D11,
  input  D21,
  input  D31,
  input  D02,
  input  D12,
  input  D22,
  input  D32,
  output Y0,
  output Y1,
  output Y2
);

  wire and_1_out, and_2_out, and_3_out, and_4_out, and_5_out, and_6_out, and_7_out, and_8_out, and_9_out,
       and_10_out, and_11_out, and_12_out, and_13_out, and_14_out, and_15_out, and_16_out, not_1_out,
       not_2_out;

  not not_1 (not_1_out, S1);
  not not_2 (not_2_out, S0);
  and and_1 (and_1_out, not_1_out, not_2_out);
  and and_2 (and_2_out, not_1_out, S0);
  and and_3 (and_3_out, S1, not_2_out);
  and and_4 (and_4_out, S1, S0);
  and and_5 (and_5_out, D00, and_1_out);
  and and_6 (and_6_out, D10, and_2_out);
  and and_7 (and_7_out, D20, and_3_out);
  and and_8 (and_8_out, D30, and_4_out);
  and and_9 (and_9_out, D01, and_1_out);
  and and_10 (and_10_out, D11, and_2_out);
  and and_11 (and_11_out, D21, and_3_out);
  and and_12 (and_12_out, D31, and_4_out);
  and and_13 (and_13_out, D02, and_1_out);
  and and_14 (and_14_out, D12, and_2_out);
  and and_15 (and_15_out, D22, and_3_out);
  and and_16 (and_16_out, D32, and_4_out);
  or or_1 (Y1, and_9_out, and_10_out, and_11_out, and_12_out);
  or or_2 (Y2, and_13_out, and_14_out, and_15_out, and_16_out);
  or or_3 (Y0, and_5_out, and_6_out, and_7_out, and_8_out);
endmodule

module Mux_1bit_4to1 (
  input  D0,
  input  S1,
  input  S0,
  input  D1,
  input  D2,
  input  D3,
  output Y
);

  wire and_1_out, and_2_out, and_3_out, and_4_out, and_5_out, and_6_out, and_7_out, and_8_out, not_1_out,
       not_2_out;

  not not_1 (not_1_out, S1);
  not not_2 (not_2_out, S0);
  and and_1 (and_1_out, not_1_out, not_2_out);
  and and_2 (and_2_out, not_1_out, S0);
  and and_3 (and_3_out, S1, not_2_out);
  and and_4 (and_4_out, S1, S0);
  and and_5 (and_5_out, D0, and_1_out);
  and and_6 (and_6_out, D1, and_2_out);
  and and_7 (and_7_out, D2, and_3_out);
  and and_8 (and_8_out, D3, and_4_out);
  or or_1 (Y, and_5_out, and_6_out, and_7_out, and_8_out);
endmodule

module Mux_4bit_2to1 (
  input  D00,
  input  D10,
  input  D01,
  input  S,
  input  D11,
  input  D02,
  input  D12,
  input  D03,
  input  D13,
  output Y0,
  output Y1,
  output Y2,
  output Y3
);

  wire and_1_out, and_2_out, and_3_out, and_4_out, and_5_out, and_6_out, and_7_out, and_8_out, not_1_out;

  not not_1 (not_1_out, S);
  and and_1 (and_1_out, D00, not_1_out);
  and and_2 (and_2_out, D10, S);
  and and_3 (and_3_out, D01, not_1_out);
  and and_4 (and_4_out, D11, S);
  and and_5 (and_5_out, D02, not_1_out);
  and and_6 (and_6_out, D12, S);
  and and_7 (and_7_out, D03, not_1_out);
  and and_8 (and_8_out, D13, S);
  or or_1 (Y0, and_1_out, and_2_out);
  or or_2 (Y1, and_3_out, and_4_out);
  or or_3 (Y2, and_5_out, and_6_out);
  or or_4 (Y3, and_7_out, and_8_out);
endmodule

module Mux_1bit_2to1 (
  input  D0,
  input  S,
  input  D1,
  output Y
);

  wire and_1_out, and_2_out, not_1_out;

  not not_1 (not_1_out, S);
  and and_1 (and_1_out, D0, not_1_out);
  and and_2 (and_2_out, S, D1);
  or or_1 (Y, and_1_out, and_2_out);
endmodule
