// Logisim project sequence_summation_circuit.circ as structural Verilog: 15 circuits, main circuit main
module main (
  input  R,
  input  EN,
  input  clk
);

  wire seg7_h_1_ya, seg7_h_1_yb, seg7_h_1_yc, seg7_h_1_yd, seg7_h_1_ye, seg7_h_1_yf, seg7_h_1_yg,
       seg7_h_2_ya, seg7_h_2_yb, seg7_h_2_yc, seg7_h_2_yd, seg7_h_2_ye, seg7_h_2_yf, seg7_h_2_yg;
  wire [3:0] register8bit_1_q0, register8bit_1_q4;
  wire [7:0] adder8bit_1_s0, adder8bit_2_s0, register8bit_2_q0;

  register8bit register8bit_1 (
    .R(R), .D0(adder8bit_1_s0[0]), .EN(EN), .clk(clk), .D1(adder8bit_1_s0[1]), .D2(adder8bit_1_s0[2]),
    .D3(adder8bit_1_s0[3]), .D4(adder8bit_1_s0[4]), .D5(adder8bit_1_s0[5]), .D6(adder8bit_1_s0[6]),
    .D7(adder8bit_1_s0[7]), .Q0(register8bit_1_q0[0]), .Q1(register8bit_1_q0[1]), .Q2(register8bit_1_q0[2]),
    .Q3(register8bit_1_q0[3]), .Q4(register8bit_1_q4[0]), .Q5(register8bit_1_q4[1]),
    .Q6(register8bit_1_q4[2]), .Q7(register8bit_1_q4[3]));  // open: Q0_bar, Q1_bar, Q2_bar, Q3_bar, Q4_bar, Q5_bar, Q6_bar, Q7_bar
  Adder8bit adder8bit_1 (
    .A0(register8bit_1_q0[0]), .A1(register8bit_1_q0[1]), .A2(register8bit_1_q0[2]),
    .A3(register8bit_1_q0[3]), .A4(register8bit_1_q4[0]), .A5(register8bit_1_q4[1]),
    .A6(register8bit_1_q4[2]), .A7(register8bit_1_q4[3]), .B0(register8bit_2_q0[0]),
    .B1(register8bit_2_q0[1]), .B2(register8bit_2_q0[2]), .B3(register8bit_2_q0[3]),
    .B4(register8bit_2_q0[4]), .B5(register8bit_2_q0[5]), .B6(register8bit_2_q0[6]),
    .B7(register8bit_2_q0[7]), .S0(adder8bit_1_s0[0]), .S1(adder8bit_1_s0[1]), .S2(adder8bit_1_s0[2]),
    .S3(adder8bit_1_s0[3]), .S4(adder8bit_1_s0[4]), .S5(adder8bit_1_s0[5]), .S6(adder8bit_1_s0[6]),
    .S7(adder8bit_1_s0[7]));  // open: C0, Cout
  register8bit register8bit_2 (
    .R(R), .D0(adder8bit_2_s0[0]), .EN(EN), .clk(clk), .D1(adder8bit_2_s0[1]), .D2(adder8bit_2_s0[2]),
    .D3(adder8bit_2_s0[3]), .D4(adder8bit_2_s0[4]), .D5(adder8bit_2_s0[5]), .D6(adder8bit_2_s0[6]),
    .D7(adder8bit_2_s0[7]), .Q0(register8bit_2_q0[0]), .Q1(register8bit_2_q0[1]), .Q2(register8bit_2_q0[2]),
    .Q3(register8bit_2_q0[3]), .Q4(register8bit_2_q0[4]), .Q5(register8bit_2_q0[5]),
    .Q6(register8bit_2_q0[6]), .Q7(register8bit_2_q0[7]));  // open: Q0_bar, Q1_bar, Q2_bar, Q3_bar, Q4_bar, Q5_bar, Q6_bar, Q7_bar
  Adder8bit adder8bit_2 (
    .C0(1'b1), .A0(register8bit_2_q0[0]), .A1(register8bit_2_q0[1]), .A2(register8bit_2_q0[2]),
    .A3(register8bit_2_q0[3]), .A4(register8bit_2_q0[4]), .A5(register8bit_2_q0[5]),
    .A6(register8bit_2_q0[6]), .A7(register8bit_2_q0[7]), .B0(1'b0), .B1(1'b0), .B2(1'b0), .B3(1'b0),
    .B4(1'b0), .B5(1'b0), .B6(1'b0), .B7(1'b0), .S0(adder8bit_2_s0[0]), .S1(adder8bit_2_s0[1]),
    .S2(adder8bit_2_s0[2]), .S3(adder8bit_2_s0[3]), .S4(adder8bit_2_s0[4]), .S5(adder8bit_2_s0[5]),
    .S6(adder8bit_2_s0[6]), .S7(adder8bit_2_s0[7]));  // open: Cout
  Seg7_H seg7_h_1 (
    .A0(register8bit_1_q0[0]), .A1(register8bit_1_q0[1]), .A2(register8bit_1_q0[2]),
    .A3(register8bit_1_q0[3]), .Yg(seg7_h_1_yg), .Yf(seg7_h_1_yf), .Ya(seg7_h_1_ya), .Yb(seg7_h_1_yb),
    .Yc(seg7_h_1_yc), .Yd(seg7_h_1_yd), .Ye(seg7_h_1_ye));
  Seg7_H seg7_h_2 (
    .A0(register8bit_1_q4[0]), .A1(register8bit_1_q4[1]), .A2(register8bit_1_q4[2]),
    .A3(register8bit_1_q4[3]), .Yg(seg7_h_2_yg), .Yf(seg7_h_2_yf), .Ya(seg7_h_2_ya), .Yb(seg7_h_2_yb),
    .Yc(seg7_h_2_yc), .Yd(seg7_h_2_yd), .Ye(seg7_h_2_ye));
  _7_Segment_Display u_7_segment_display_1 (
    .g(seg7_h_1_yg), .f(seg7_h_1_yf), .a(seg7_h_1_ya), .b(seg7_h_1_yb), .e(seg7_h_1_ye), .d(seg7_h_1_yd),
    .c(seg7_h_1_yc));  // open: dp
  _7_Segment_Display u_7_segment_display_2 (
    .g(seg7_h_2_yg), .f(seg7_h_2_yf), .a(seg7_h_2_ya), .b(seg7_h_2_yb), .e(seg7_h_2_ye), .d(seg7_h_2_yd),
    .c(seg7_h_2_yc));  // open: dp
endmodule

module Seg7_H (
  input  A0,
  input  A1,
  input  A2,
  input  A3,
  output Yg,
  output Yf,
  output Ya,
  output Yb,
  output Yc,
  output Yd,
  output Ye
);

  wire decoder_416_1_y0, decoder_416_1_y1, decoder_416_1_y2, decoder_416_1_y3, decoder_416_1_y4,
       decoder_416_1_y5, decoder_416_1_y6, decoder_416_1_y7, decoder_416_1_y8, decoder_416_1_y9,
       decoder_416_1_y10, decoder_416_1_y11, decoder_416_1_y12, decoder_416_1_y13, decoder_416_1_y14,
       decoder_416_1_y15;

  decoder_416 decoder_416_1 (
    .A0(A0), .A1(A1), .A2(A2), .A3(A3), .Y0(decoder_416_1_y0), .Y1(decoder_416_1_y1), .Y2(decoder_416_1_y2),
    .Y3(decoder_416_1_y3), .Y4(decoder_416_1_y4), .Y5(decoder_416_1_y5), .Y6(decoder_416_1_y6),
    .Y7(decoder_416_1_y7), .Y8(decoder_416_1_y8), .Y9(decoder_416_1_y9), .Y10(decoder_416_1_y10),
    .Y11(decoder_416_1_y11), .Y12(decoder_416_1_y12), .Y13(decoder_416_1_y13), .Y14(decoder_416_1_y14),
    .Y15(decoder_416_1_y15));
  or g (Yg, decoder_416_1_y2, decoder_416_1_y3, decoder_416_1_y4, decoder_416_1_y5, decoder_416_1_y6, decoder_416_1_y8, decoder_416_1_y9, decoder_416_1_y10, decoder_416_1_y11, decoder_416_1_y13, decoder_416_1_y14, decoder_416_1_y15);
  or f (Yf, decoder_416_1_y0, decoder_416_1_y4, decoder_416_1_y5, decoder_416_1_y6, decoder_416_1_y8, decoder_416_1_y9, decoder_416_1_y10, decoder_416_1_y11, decoder_416_1_y12, decoder_416_1_y14, decoder_416_1_y15);
  or a (Ya, decoder_416_1_y0, decoder_416_1_y2, decoder_416_1_y3, decoder_416_1_y5, decoder_416_1_y6, decoder_416_1_y7, decoder_416_1_y8, decoder_416_1_y9, decoder_416_1_y10, decoder_416_1_y12, decoder_416_1_y14, decoder_416_1_y15);
  or b (Yb, decoder_416_1_y0, decoder_416_1_y1, decoder_416_1_y2, decoder_416_1_y3, decoder_416_1_y4, decoder_416_1_y7, decoder_416_1_y8, decoder_416_1_y9, decoder_416_1_y10, decoder_416_1_y13);
  or c (Yc, decoder_416_1_y0, decoder_416_1_y1, decoder_416_1_y3, decoder_416_1_y4, decoder_416_1_y5, decoder_416_1_y6, decoder_416_1_y7, decoder_416_1_y8, decoder_416_1_y9, decoder_416_1_y10, decoder_416_1_y11, decoder_416_1_y13);
  or d (Yd, decoder_416_1_y0, decoder_416_1_y2, decoder_416_1_y3, decoder_416_1_y5, decoder_416_1_y6, decoder_416_1_y8, decoder_416_1_y9, decoder_416_1_y11, decoder_416_1_y12, decoder_416_1_y13, decoder_416_1_y14);
  or e (Ye, decoder_416_1_y0, decoder_416_1_y2, decoder_416_1_y6, decoder_416_1_y8, decoder_416_1_y10, decoder_416_1_y11, decoder_416_1_y12, decoder_416_1_y13, decoder_416_1_y14, decoder_416_1_y15);
endmodule

module decoder_24 (
  input  A0,
  input  A1,
  output Y0,
  output Y1,
  output Y2,
  output Y3
);

  wire not_1_out, not_2_out;

  not not_1 (not_1_out, A0);
  not not_2 (not_2_out, A1);
  and and_1 (Y0, not_1_out, not_2_out);
  and and_2 (Y1, A0, not_2_out);
  and and_3 (Y2, not_1_out, A1);
  and and_4 (Y3, A0, A1);
endmodule

module decoder_38 (
  input  A0,
  input  A1,
  input  A2,
  output Y0,
  output Y1,
  output Y2,
  output Y3,
  output Y4,
  output Y5,
  output Y6,
  output Y7
);

  wire decoder_24_1_y0, decoder_24_1_y1, decoder_24_1_y2, decoder_24_1_y3, not_1_out;

  not not_1 (not_1_out, A2);
  decoder_24 decoder_24_1 (
    .A0(A0), .A1(A1), .Y0(decoder_24_1_y0), .Y1(decoder_24_1_y1), .Y2(decoder_24_1_y2), .Y3(decoder_24_1_y3));
  and and_1 (Y0, decoder_24_1_y0, not_1_out);
  and and_2 (Y1, decoder_24_1_y1, not_1_out);
  and and_3 (Y2, decoder_24_1_y2, not_1_out);
  and and_4 (Y3, decoder_24_1_y3, not_1_out);
  and and_5 (Y4, decoder_24_1_y0, A2);
  and and_6 (Y5, decoder_24_1_y1, A2);
  and and_7 (Y6, decoder_24_1_y2, A2);
  and and_8 (Y7, decoder_24_1_y3, A2);
endmodule

module decoder_416 (
  input  A0,
  input  A1,
  input  A2,
  input  A3,
  output Y0,
  output Y1,
  output Y2,
  output Y3,
  output Y4,
  output Y5,
  output Y6,
  output Y7,
  output Y8,
  output Y9,
  output Y10,
  output Y11,
  output Y12,
  output Y13,
  output Y14,
  output Y15
);

  wire decoder_38_1_y0, decoder_38_1_y1, decoder_38_1_y2, decoder_38_1_y3, decoder_38_1_y4, decoder_38_1_y5,
       decoder_38_1_y6, decoder_38_1_y7, not_1_out;

  not not_1 (not_1_out, A3);
  decoder_38 decoder_38_1 (
    .A0(A0), .A1(A1), .A2(A2), .Y0(decoder_38_1_y0), .Y1(decoder_38_1_y1), .Y2(decoder_38_1_y2),
    .Y3(decoder_38_1_y3), .Y4(decoder_38_1_y4), .Y5(decoder_38_1_y5), .Y6(decoder_38_1_y6),
    .Y7(decoder_38_1_y7));
  and and_1 (Y0, decoder_38_1_y0, not_1_out);
  and and_2 (Y1, decoder_38_1_y1, not_1_out);
  and and_3 (Y2, decoder_38_1_y2, not_1_out);
  and and_4 (Y3, decoder_38_1_y3, not_1_out);
  and and_5 (Y4, decoder_38_1_y4, not_1_out);
  and and_6 (Y5, decoder_38_1_y5, not_1_out);
  and and_7 (Y6, decoder_38_1_y6, not_1_out);
  and and_8 (Y7, decoder_38_1_y7, not_1_out);
  and and_9 (Y8, decoder_38_1_y0, A3);
  and and_10 (Y9, decoder_38_1_y1, A3);
  and and_11 (Y10, decoder_38_1_y2, A3);
  and and_12 (Y11, decoder_38_1_y3, A3);
  and and_13 (Y12, decoder_38_1_y4, A3);
  and and_14 (Y13, decoder_38_1_y5, A3);
  and and_15 (Y14, decoder_38_1_y6, A3);
  and and_16 (Y15, decoder_38_1_y7, A3);
endmodule

module SR_latch_NOR (
  input  R,
  input  S,
  output Q,
  output Q_bar
);

  nor nor_1 (Q, R, Q_bar);
  nor nor_2 (Q_bar, S, Q);
endmodule

module D_latch (
  input  R,
  input  WE,
  input  D,
  output Q,
  output Q_bar
);

  wire and_1_out, and_2_out, not_1_out, not_2_out, or_1_out;

  not not_1 (not_1_out, R);
  not not_2 (not_2_out, D);
  and and_1 (and_1_out, not_1_out, D, WE);
  and and_2 (and_2_out, WE, not_2_out);
  or or_1 (or_1_out, R, and_2_out);
  SR_latch_NOR sr_latch_nor_1 (.R(or_1_out), .S(and_1_out), .Q(Q), .Q_bar(Q_bar));
endmodule

module DFF (
  input  R,
  input  D,
  input  clk,
  output Q,
  output Q_bar
);

  wire d_latch_1_q, not_1_out;

  not not_1 (not_1_out, clk);
  D_latch d_latch_1 (.R(R), .WE(not_1_out), .D(D), .Q(d_latch_1_q));  // open: Q_bar
  D_latch d_latch_2 (.R(R), .WE(clk), .D(d_latch_1_q), .Q(Q), .Q_bar(Q_bar));
endmodule

module DFF_EN (
  input  R,
  input  D,
  input  clk,
  input  EN,
  output Q,
  output Q_bar
);

  wire multiplexer_1_out;

  Multiplexer multiplexer_1 (.in0(Q), .in1(D), .out(multiplexer_1_out), .sel(EN));
  DFF dff_1 (.R(R), .D(multiplexer_1_out), .clk(clk), .Q(Q), .Q_bar(Q_bar));
endmodule

module register4bit (
  input  R,
  input  D0,
  input  EN,
  input  clk,
  input  D1,
  input  D2,
  input  D3,
  output Q0,
  output Q0_bar,
  output Q1,
  output Q1_bar,
  output Q2,
  output Q2_bar,
  output Q3,
  output Q3_bar
);

  DFF_EN dff_en_1 (.R(R), .D(D0), .clk(clk), .EN(EN), .Q(Q0), .Q_bar(Q0_bar));
  DFF_EN dff_en_2 (.R(R), .D(D1), .clk(clk), .EN(EN), .Q(Q1), .Q_bar(Q1_bar));
  DFF_EN dff_en_3 (.R(R), .D(D2), .clk(clk), .EN(EN), .Q(Q2), .Q_bar(Q2_bar));
  DFF_EN dff_en_4 (.R(R), .D(D3), .clk(clk), .EN(EN), .Q(Q3), .Q_bar(Q3_bar));
endmodule

module register8bit (
  input  R,
  input  D0,
  input  EN,
  input  clk,
  input  D1,
  input  D2,
  input  D3,
  input  D4,
  input  D5,
  input  D6,
  input  D7,
  output Q0,
  output Q0_bar,
  output Q1,
  output Q1_bar,
  output Q2,
  output Q2_bar,
  output Q3,
  output Q3_bar,
  output Q4,
  output Q4_bar,
  output Q5,
  output Q5_bar,
  output Q6,
  output Q6_bar,
  output Q7,
  output Q7_bar
);

  DFF_EN dff_en_1 (.R(R), .D(D0), .clk(clk), .EN(EN), .Q(Q0), .Q_bar(Q0_bar));
  DFF_EN dff_en_2 (.R(R), .D(D1), .clk(clk), .EN(EN), .Q(Q1), .Q_bar(Q1_bar));
  DFF_EN dff_en_3 (.R(R), .D(D2), .clk(clk), .EN(EN), .Q(Q2), .Q_bar(Q2_bar));
  DFF_EN dff_en_4 (.R(R), .D(D3), .clk(clk), .EN(EN), .Q(Q3), .Q_bar(Q3_bar));
  DFF_EN dff_en_5 (.R(R), .D(D4), .clk(clk), .EN(EN), .Q(Q4), .Q_bar(Q4_bar));
  DFF_EN dff_en_6 (.R(R), .D(D5), .clk(clk), .EN(EN), .Q(Q5), .Q_bar(Q5_bar));
  DFF_EN dff_en_7 (.R(R), .D(D6), .clk(clk), .EN(EN), .Q(Q6), .Q_bar(Q6_bar));
  DFF_EN dff_en_8 (.R(R), .D(D7), .clk(clk), .EN(EN), .Q(Q7), .Q_bar(Q7_bar));
endmodule

module Add_2 (
  input  A,
  input  B,
  input  Cin,
  output Sum,
  output Cout
);

  wire half_add_1_c, half_add_1_s, half_add_2_c;

  half_add half_add_1 (.A(A), .B(B), .S(half_add_1_s), .C(half_add_1_c));
  half_add half_add_2 (.A(half_add_1_s), .B(Cin), .S(Sum), .C(half_add_2_c));
  or or_1 (Cout, half_add_1_c, half_add_2_c);
endmodule

module half_add (
  input  A,
  input  B,
  output S,
  output C
);

  xor xor_1 (S, A, B);
  and and_1 (C, A, B);
endmodule

module Adder4bit (
  input  A0,
  input  A1,
  input  A2,
  input  A3,
  input  B0,
  input  B1,
  input  B2,
  input  B3,
  input  C0,
  output S0,
  output S1,
  output S2,
  output S3,
  output C4
);

  wire add_2_1_cout, add_2_2_cout, add_2_3_cout, seg7_h_1_ya, seg7_h_1_yb, seg7_h_1_yc, seg7_h_1_yd,
       seg7_h_1_ye, seg7_h_1_yf, seg7_h_1_yg, seg7_h_2_ya, seg7_h_2_yb, seg7_h_2_yc, seg7_h_2_yd,
       seg7_h_2_ye, seg7_h_2_yf, seg7_h_2_yg, seg7_h_3_ya, seg7_h_3_yb, seg7_h_3_yc, seg7_h_3_yd,
       seg7_h_3_ye, seg7_h_3_yf, seg7_h_3_yg;

  Seg7_H seg7_h_1 (
    .A0(A0), .A1(A1), .A2(A2), .A3(A3), .Yg(seg7_h_1_yg), .Yf(seg7_h_1_yf), .Ya(seg7_h_1_ya),
    .Yb(seg7_h_1_yb), .Yc(seg7_h_1_yc), .Yd(seg7_h_1_yd), .Ye(seg7_h_1_ye));
  Seg7_H seg7_h_2 (
    .A0(B0), .A1(B1), .A2(B2), .A3(B3), .Yg(seg7_h_2_yg), .Yf(seg7_h_2_yf), .Ya(seg7_h_2_ya),
    .Yb(seg7_h_2_yb), .Yc(seg7_h_2_yc), .Yd(seg7_h_2_yd), .Ye(seg7_h_2_ye));
  Add_2 add_2_1 (.A(A0), .B(B0), .Cin(C0), .Sum(S0), .Cout(add_2_1_cout));
  Add_2 add_2_2 (.A(A1), .B(B1), .Cin(add_2_1_cout), .Sum(S1), .Cout(add_2_2_cout));
  Add_2 add_2_3 (.A(A2), .B(B2), .Cin(add_2_2_cout), .Sum(S2), .Cout(add_2_3_cout));
  Add_2 add_2_4 (.A(A3), .B(B3), .Cin(add_2_3_cout), .Sum(S3), .Cout(C4));
  _7_Segment_Display u_7_segment_display_1 (
    .g(seg7_h_1_yg), .f(seg7_h_1_yf), .a(seg7_h_1_ya), .b(seg7_h_1_yb), .e(seg7_h_1_ye), .d(seg7_h_1_yd),
    .c(seg7_h_1_yc));  // open: dp
  _7_Segment_Display u_7_segment_display_2 (
    .g(seg7_h_2_yg), .f(seg7_h_2_yf), .a(seg7_h_2_ya), .b(seg7_h_2_yb), .e(seg7_h_2_ye), .d(seg7_h_2_yd),
    .c(seg7_h_2_yc));  // open: dp
  LED led_1 (.in(C4));
  Seg7_H seg7_h_3 (
    .A0(S0), .A1(S1), .A2(S2), .A3(S3), .Yg(seg7_h_3_yg), .Yf(seg7_h_3_yf), .Ya(seg7_h_3_ya),
    .Yb(seg7_h_3_yb), .Yc(seg7_h_3_yc), .Yd(seg7_h_3_yd), .Ye(seg7_h_3_ye));
  _7_Segment_Display u_7_segment_display_3 (
    .g(seg7_h_3_yg), .f(seg7_h_3_yf), .a(seg7_h_3_ya), .b(seg7_h_3_yb), .e(seg7_h_3_ye), .d(seg7_h_3_yd),
    .c(seg7_h_3_yc));  // open: dp
endmodule

module Adder8bit (
  input  C0,
  input  A0,
  input  A1,
  input  A2,
  input  A3,
  input  A4,
  input  A5,
  input  A6,
  input  A7,
  input  B0,
  input  B1,
  input  B2,
  input  B3,
  input  B4,
  input  B5,
  input  B6,
  input  B7,
  output S0,
  output S1,
  output S2,
  output S3,
  output S4,
  output S5,
  output S6,
  output S7,
  output Cout
);

  wire add_2_1_cout, add_2_2_cout, add_2_3_cout, add_2_4_cout, add_2_5_cout, add_2_6_cout, add_2_7_cout;

  Add_2 add_2_1 (.A(A0), .B(B0), .Cin(C0), .Sum(S0), .Cout(add_2_1_cout));
  Add_2 add_2_2 (.A(A1), .B(B1), .Cin(add_2_1_cout), .Sum(S1), .Cout(add_2_2_cout));
  Add_2 add_2_3 (.A(A2), .B(B2), .Cin(add_2_2_cout), .Sum(S2), .Cout(add_2_3_cout));
  Add_2 add_2_4 (.A(A3), .B(B3), .Cin(add_2_3_cout), .Sum(S3), .Cout(add_2_4_cout));
  Add_2 add_2_5 (.A(A4), .B(B4), .Cin(add_2_4_cout), .Sum(S4), .Cout(add_2_5_cout));
  Add_2 add_2_6 (.A(A5), .B(B5), .Cin(add_2_5_cout), .Sum(S5), .Cout(add_2_6_cout));
  Add_2 add_2_7 (.A(A6), .B(B6), .Cin(add_2_6_cout), .Sum(S6), .Cout(add_2_7_cout));
  Add_2 add_2_8 (.A(A7), .B(B7), .Cin(add_2_7_cout), .Sum(S7), .Cout(Cout));
endmodule
