// Logisim project add_sCPU.circ as structural Verilog: 1 circuit, main circuit main
module main (
  input  in_1
);

  wire and_1_out, and_2_out, and_3_out, and_4_out, clk_out, decoder_1_out0, decoder_1_out2, decoder_2_out0,
       decoder_2_out1, decoder_2_out2, decoder_2_out3, or_1_out, or_2_out;
  wire [2:0] adder_1_out, PC_q;
  wire [7:0] adder_2_out, multiplexer_1_out, multiplexer_2_out, multiplexer_3_out, multiplexer_4_out, r0_q,
       r1_q, r2_q, r3_q;

  Adder #(.width(3)) adder_1 (.a(PC_q), .b(3'b001), .out(adder_1_out));  // open: cin, cout
  Register #(.width(3)) PC (.D(adder_1_out), .en(1'b1), .clk(clk_out), .Q(PC_q), .clr(in_1));
  Clock clk (.out(clk_out));
  Multiplexer #(.select(3), .width(8)) multiplexer_1 (
    .in0(8'h8a), .in1(8'h90), .in2(8'ha0), .in3(8'hb1), .in4(8'h17), .in5(8'h29), .in6(8'hd1), .in7(8'hdf),
    .out(multiplexer_1_out), .sel(PC_q));
  Decoder #(.enable("false"), .select(2)) decoder_1 (
    .out0(decoder_1_out0), .out2(decoder_1_out2), .sel(multiplexer_1_out[7:6]));  // open: out1, out3
  or or_1 (or_1_out, decoder_1_out0, decoder_1_out2);
  Multiplexer #(.select(2), .width(8)) multiplexer_2 (
    .in0(adder_2_out), .in2({4'b0000, multiplexer_1_out[3:0]}), .out(multiplexer_2_out),
    .sel(multiplexer_1_out[7:6]));  // open: in1, in3
  or or_2 (or_2_out, decoder_1_out0, decoder_1_out2);
  Decoder #(.select(2)) decoder_2 (
    .out0(decoder_2_out0), .out1(decoder_2_out1), .out2(decoder_2_out2), .out3(decoder_2_out3),
    .sel(multiplexer_1_out[5:4]), .en(or_2_out));
  and and_1 (and_1_out, or_1_out, decoder_2_out0);
  Register r0 (.D(multiplexer_2_out), .en(and_1_out), .clk(clk_out), .Q(r0_q));  // open: clr
  Multiplexer #(.enable("true"), .select(2), .width(8)) multiplexer_3 (
    .in0(r0_q), .in1(r1_q), .in2(r2_q), .in3(r3_q), .out(multiplexer_3_out), .sel(multiplexer_1_out[3:2]),
    .en(decoder_1_out0));
  Register r1 (.D(multiplexer_2_out), .en(and_2_out), .clk(clk_out), .Q(r1_q));  // open: clr
  and and_2 (and_2_out, or_1_out, decoder_2_out1);
  Multiplexer #(.enable("true"), .select(2), .width(8)) multiplexer_4 (
    .in0(r0_q), .in1(r1_q), .in2(r2_q), .in3(r3_q), .out(multiplexer_4_out), .sel(multiplexer_1_out[1:0]),
    .en(decoder_1_out0));
  Adder adder_2 (.a(multiplexer_4_out), .b(multiplexer_3_out), .out(adder_2_out));  // open: cin, cout
  Register r2 (.D(multiplexer_2_out), .en(and_3_out), .clk(clk_out), .Q(r2_q));  // open: clr
  and and_3 (and_3_out, or_1_out, decoder_2_out2);
  Register r3 (.D(multiplexer_2_out), .en(and_4_out), .clk(clk_out), .Q(r3_q));  // open: clr
  and and_4 (and_4_out, or_1_out, decoder_2_out3);
endmodule
