// Logisim project execute.circ as structural Verilog: 1 circuit, main circuit main
module main (
  input  [7:0] D,
  input  EN,
  input  [1:0] addr,
  output [7:0] out_4
);

  wire and_1_out, and_2_out, and_3_out, and_4_out, clk_out, decoder_1_out0, decoder_1_out1, decoder_1_out2,
       decoder_1_out3;
  wire [7:0] r0_q, r1_q, r2_q, r3_q;

  Clock clk (.out(clk_out));
  Decoder #(.select(2)) decoder_1 (
    .out0(decoder_1_out0), .out1(decoder_1_out1), .out2(decoder_1_out2), .out3(decoder_1_out3), .sel(addr));  // open: en
  Register r0 (.D(D), .en(and_1_out), .clk(clk_out), .Q(r0_q));  // open: clr
  and and_1 (and_1_out, EN, decoder_1_out0);
  and and_2 (and_2_out, EN, decoder_1_out1);
  Register r1 (.D(D), .en(and_2_out), .clk(clk_out), .Q(r1_q));  // open: clr
  Multiplexer #(.select(2), .width(8)) multiplexer_1 (
    .in0(r0_q), .in1(r1_q), .in2(r2_q), .in3(r3_q), .out(out_4), .sel(addr));
  and and_3 (and_3_out, EN, decoder_1_out2);
  Register r2 (.D(D), .en(and_3_out), .clk(clk_out), .Q(r2_q));  // open: clr
  and and_4 (and_4_out, EN, decoder_1_out3);
  Register r3 (.D(D), .en(and_4_out), .clk(clk_out), .Q(r3_q));  // open: clr
endmodule
