// Logisim project sCPU_the_sum_of_odd_numbers10.circ as structural Verilog: 1 circuit, main circuit main
module main (
  input  in_1
);

  wire and_1_out, and_2_out, and_3_out, and_4_out, and_5_out, clk_out, comparator_1_eq, decoder_1_out0,
       decoder_1_out2, decoder_1_out3, decoder_2_out0, decoder_2_out1, decoder_2_out2, decoder_2_out3,
       not_1_out, or_1_out, or_2_out, or_3_out;
  wire [1:0] multiplexer_4_out;
  wire [3:0] adder_1_out, multiplexer_1_out, multiplexer_2_out, PC_q;
  wire [7:0] adder_2_out, multiplexer_2_out_2, multiplexer_3_out, multiplexer_5_out, multiplexer_6_out, r0_q,
       r1_q, r2_q, r3_q;

  Adder #(.width(4)) adder_1 (.a(PC_q), .b(4'b0001), .out(adder_1_out));  // open: cin, cout
  Clock clk (.out(clk_out));
  and and_1 (and_1_out, not_1_out, decoder_1_out3);
  Multiplexer #(.width(4)) multiplexer_1 (
    .in0(adder_1_out), .in1(multiplexer_2_out), .out(multiplexer_1_out), .sel(and_1_out));
  Register #(.width(4)) PC (.D(multiplexer_1_out), .en(1'b1), .clk(clk_out), .Q(PC_q), .clr(in_1));
  Multiplexer #(.select(4), .width(8)) multiplexer_2 (
    .in0(8'h8b), .in1(8'h91), .in2(8'ha0), .in3(8'hb2), .in4(8'h29), .in5(8'h17), .in6(8'hd1), .in7(8'hdf),
    .out({multiplexer_2_out_2[7:6], multiplexer_2_out, multiplexer_2_out_2[1:0]}), .sel(PC_q));  // open: in8, in9, in10, in11, in12, in13, in14, in15
  Decoder #(.select(2)) decoder_1 (
    .out0(decoder_1_out0), .out2(decoder_1_out2), .out3(decoder_1_out3), .sel(multiplexer_2_out_2[7:6]));  // open: out1, en
  or or_1 (or_1_out, decoder_1_out0, decoder_1_out3);
  or or_2 (or_2_out, decoder_1_out0, decoder_1_out2);
  or or_3 (or_3_out, decoder_1_out0, decoder_1_out2);
  Multiplexer #(.select(2), .width(8)) multiplexer_3 (
    .in0(adder_2_out), .in2({4'b0000, multiplexer_2_out[1:0], multiplexer_2_out_2[1:0]}),
    .out(multiplexer_3_out), .sel(multiplexer_2_out_2[7:6]));  // open: in1, in3
  Decoder #(.select(2)) decoder_2 (
    .out0(decoder_2_out0), .out1(decoder_2_out1), .out2(decoder_2_out2), .out3(decoder_2_out3),
    .sel(multiplexer_2_out[3:2]), .en(or_3_out));
  and and_2 (and_2_out, or_2_out, decoder_2_out0);
  Register r0 (.D(multiplexer_3_out), .en(and_2_out), .clk(clk_out), .Q(r0_q));  // open: clr
  Multiplexer #(.select(2), .width(2)) multiplexer_4 (
    .in0(multiplexer_2_out[1:0]), .in3(2'b00), .out(multiplexer_4_out), .sel(multiplexer_2_out_2[7:6]));  // open: in1, in2
  Multiplexer #(.enable("true"), .select(2), .width(8)) multiplexer_5 (
    .in0(r0_q), .in1(r1_q), .in2(r2_q), .in3(r3_q), .out(multiplexer_5_out), .sel(multiplexer_4_out),
    .en(or_1_out));
  Register r1 (.D(multiplexer_3_out), .en(and_3_out), .clk(clk_out), .Q(r1_q));  // open: clr
  and and_3 (and_3_out, or_2_out, decoder_2_out1);
  Multiplexer #(.enable("true"), .select(2), .width(8)) multiplexer_6 (
    .in0(r0_q), .in1(r1_q), .in2(r2_q), .in3(r3_q), .out(multiplexer_6_out), .sel(multiplexer_2_out_2[1:0]),
    .en(or_1_out));
  Register r2 (.D(multiplexer_3_out), .en(and_4_out), .clk(clk_out), .Q(r2_q));  // open: clr
  and and_4 (and_4_out, or_2_out, decoder_2_out2);
  Adder adder_2 (.a(multiplexer_6_out), .b(multiplexer_5_out), .out(adder_2_out));  // open: cin, cout
  not not_1 (not_1_out, comparator_1_eq);
  Comparator comparator_1 (.a(multiplexer_6_out), .b(multiplexer_5_out), .eq(comparator_1_eq));  // open: gt, lt
  Register r3 (.D(multiplexer_3_out), .en(and_5_out), .clk(clk_out), .Q(r3_q));  // open: clr
  and and_5 (and_5_out, or_2_out, decoder_2_out3);

  // Notes on the sheet:
  //   rs2
  //   rs1
endmodule
