// Logisim project Enhanced_version_of_sCPU.circ as structural Verilog
module Finger_Pricking (
  input  [3:0] in_1,
  output [7:0] out_2
);

  wire clock_1_out;
  wire [3:0] PC_q;

  Clock clock_1 (.out(clock_1_out));
  Register #(.width(4)) PC (.D(in_1), .en(1'b1), .clk(clock_1_out), .Q(PC_q));  // open: clr
  Multiplexer #(.select(4), .width(8)) multiplexer_1 (
    .in0(8'h86), .in1(8'h92), .in2(8'h1), .in3(8'h90), .in4(8'ha0), .in5(8'hb1), .in6(8'h17), .in7(8'h29),
    .in8(8'hf9), .in9(8'hc3), .out(out_2), .sel(PC_q));  // open: in10, in11, in12, in13, in14, in15
endmodule

module execute (
  input  [7:0] D,
  input  EN,
  input  [1:0] addr,
  output [7:0] out_4
);

  wire and_1_out, and_2_out, and_3_out, and_4_out, clk_out, decoder_1_out0, decoder_1_out1, decoder_1_out2,
       decoder_1_out3;
  wire [7:0] r0_q, r1_q, r2_q, r3_q;

  Clock clk (.out(clk_out));
  Decoder #(.select(2)) decoder_1 (
    .out0(decoder_1_out0), .out1(decoder_1_out1), .out2(decoder_1_out2), .out3(decoder_1_out3), .sel(addr));  // open: en
  Register r0 (.D(D), .en(and_1_out), .clk(clk_out), .Q(r0_q));  // open: clr
  and and_1 (and_1_out, EN, decoder_1_out0);
  and and_2 (and_2_out, EN, decoder_1_out1);
  Register r1 (.D(D), .en(and_2_out), .clk(clk_out), .Q(r1_q));  // open: clr
  Multiplexer #(.select(2), .width(8)) multiplexer_1 (
    .in0(r0_q), .in1(r1_q), .in2(r2_q), .in3(r3_q), .out(out_4), .sel(addr));
  and and_3 (and_3_out, EN, decoder_1_out2);
  Register r2 (.D(D), .en(and_3_out), .clk(clk_out), .Q(r2_q));  // open: clr
  and and_4 (and_4_out, EN, decoder_1_out3);
  Register r3 (.D(D), .en(and_4_out), .clk(clk_out), .Q(r3_q));  // open: clr
endmodule

module li_sCPU (
  input  Reset,
  output [7:0] out_2
);

  wire and_1_out, and_2_out, and_3_out, and_4_out, clk_out, decoder_1_out0, decoder_1_out1, decoder_1_out2,
       decoder_1_out3, xor_1_out;
  wire [3:0] adder_1_out, PC_q;
  wire [7:0] multiplexer_1_out, r0_q, r1_q, r2_q, r3_q, shifter_1_out;

  Adder #(.width(4)) adder_1 (.a(PC_q), .b(4'b0001), .out(adder_1_out));  // open: cin, cout
  Clock clk (.out(clk_out));
  Register #(.width(4)) PC (.D(adder_1_out), .en(1'b1), .clk(clk_out), .Q(PC_q), .clr(Reset));
  Multiplexer #(.select(4), .width(8)) multiplexer_1 (
    .in0(8'h86), .in1(8'h92), .in2(8'h1), .in3(8'h90), .in4(8'ha0), .in5(8'hb1), .in6(8'h17), .in7(8'h29),
    .in8(8'hf9), .in9(8'hc3), .out(multiplexer_1_out), .sel(PC_q));  // open: in10, in11, in12, in13, in14, in15
  xor xor_1 (xor_1_out, multiplexer_1_out[6], multiplexer_1_out[7]);
  Decoder #(.select(2)) decoder_1 (
    .out0(decoder_1_out0), .out1(decoder_1_out1), .out2(decoder_1_out2), .out3(decoder_1_out3),
    .sel(multiplexer_1_out[5:4]));  // open: en
  Shifter shifter_1 (
    .in({{6{1'b0}}, multiplexer_1_out[1:0]}), .\dist ({multiplexer_1_out[3:2], 1'b0}), .out(shifter_1_out));
  and and_1 (and_1_out, xor_1_out, decoder_1_out0);
  Register r0 (.D(shifter_1_out), .en(and_1_out), .clk(clk_out), .Q(r0_q));  // open: clr
  and and_2 (and_2_out, xor_1_out, decoder_1_out1);
  Register r1 (.D(shifter_1_out), .en(and_2_out), .clk(clk_out), .Q(r1_q));  // open: clr
  Multiplexer #(.select(2), .width(8)) multiplexer_2 (
    .in0(r0_q), .in1(r1_q), .in2(r2_q), .in3(r3_q), .out(out_2), .sel(multiplexer_1_out[5:4]));
  Register r2 (.D(shifter_1_out), .en(and_3_out), .clk(clk_out), .Q(r2_q));  // open: clr
  and and_3 (and_3_out, xor_1_out, decoder_1_out2);
  Register r3 (.D(shifter_1_out), .en(and_4_out), .clk(clk_out), .Q(r3_q));  // open: clr
  and and_4 (and_4_out, xor_1_out, decoder_1_out3);
endmodule

module add_sCPU (
  input  Reset
);

  wire and_1_out, and_2_out, and_3_out, and_4_out, clk_out, decoder_1_out0, decoder_1_out2, decoder_2_out0,
       decoder_2_out1, decoder_2_out2, decoder_2_out3, or_1_out, or_2_out;
  wire [3:0] adder_1_out, PC_q;
  wire [7:0] adder_2_out, multiplexer_1_out, multiplexer_2_out, multiplexer_3_out, multiplexer_4_out, r0_q,
       r1_q, r2_q, r3_q, shifter_1_out;

  Adder #(.width(4)) adder_1 (.a(PC_q), .b(4'b0001), .out(adder_1_out));  // open: cin, cout
  Clock clk (.out(clk_out));
  Register #(.width(4)) PC (.D(adder_1_out), .en(1'b1), .clk(clk_out), .Q(PC_q), .clr(Reset));
  Multiplexer #(.select(4), .width(8)) multiplexer_1 (
    .in0(8'h86), .in1(8'h92), .in2(8'h1), .in3(8'h90), .in4(8'ha0), .in5(8'hb1), .in6(8'h17), .in7(8'h29),
    .in8(8'hf9), .in9(8'hc3), .out(multiplexer_1_out), .sel(PC_q));  // open: in10, in11, in12, in13, in14, in15
  Decoder #(.enable("false"), .select(2)) decoder_1 (
    .out0(decoder_1_out0), .out2(decoder_1_out2), .sel(multiplexer_1_out[7:6]));  // open: out1, out3
  or or_1 (or_1_out, decoder_1_out0, decoder_1_out2);
  or or_2 (or_2_out, decoder_1_out0, decoder_1_out2);
  Shifter shifter_1 (
    .in({{6{1'b0}}, multiplexer_1_out[1:0]}), .\dist ({multiplexer_1_out[3:2], 1'b0}), .out(shifter_1_out));
  Decoder #(.select(2)) decoder_2 (
    .out0(decoder_2_out0), .out1(decoder_2_out1), .out2(decoder_2_out2), .out3(decoder_2_out3),
    .sel(multiplexer_1_out[5:4]), .en(or_2_out));
  and and_1 (and_1_out, or_1_out, decoder_2_out0);
  Multiplexer #(.select(2), .width(8)) multiplexer_2 (
    .in0(adder_2_out), .in2(shifter_1_out), .out(multiplexer_2_out), .sel(multiplexer_1_out[7:6]));  // open: in1, in3
  Register r0 (.D(multiplexer_2_out), .en(and_1_out), .clk(clk_out), .Q(r0_q));  // open: clr
  Multiplexer #(.enable("true"), .select(2), .width(8)) multiplexer_3 (
    .in0(r0_q), .in1(r1_q), .in2(r2_q), .in3(r3_q), .out(multiplexer_3_out), .sel(multiplexer_1_out[3:2]),
    .en(decoder_1_out0));
  and and_2 (and_2_out, or_1_out, decoder_2_out1);
  Register r1 (.D(multiplexer_2_out), .en(and_2_out), .clk(clk_out), .Q(r1_q));  // open: clr
  Multiplexer #(.enable("true"), .select(2), .width(8)) multiplexer_4 (
    .in0(r0_q), .in1(r1_q), .in2(r2_q), .in3(r3_q), .out(multiplexer_4_out), .sel(multiplexer_1_out[1:0]),
    .en(decoder_1_out0));
  Adder adder_2 (.a(multiplexer_4_out), .b(multiplexer_3_out), .out(adder_2_out));  // open: cin, cout
  Register r2 (.D(multiplexer_2_out), .en(and_3_out), .clk(clk_out), .Q(r2_q));  // open: clr
  and and_3 (and_3_out, or_1_out, decoder_2_out2);
  Register r3 (.D(multiplexer_2_out), .en(and_4_out), .clk(clk_out), .Q(r3_q));  // open: clr
  and and_4 (and_4_out, or_1_out, decoder_2_out3);
endmodule

module bner0_sCPU (
  input  Reset
);

  wire and_1_out, and_2_out, and_3_out, and_4_out, and_5_out, clk_out, comparator_1_eq, decoder_1_out0,
       decoder_1_out2, decoder_1_out3, decoder_2_out0, decoder_2_out1, decoder_2_out2, decoder_2_out3,
       not_1_out, or_1_out, or_2_out, or_3_out;
  wire [1:0] multiplexer_4_out;
  wire [3:0] adder_1_out, multiplexer_1_out, PC_q;
  wire [7:0] adder_2_out, multiplexer_2_out, multiplexer_3_out, multiplexer_5_out, multiplexer_6_out, r0_q,
       r1_q, r2_q, r3_q, shifter_1_out;

  Multiplexer #(.width(4)) multiplexer_1 (
    .in0(4'b0001), .in1(multiplexer_2_out[5:2]), .out(multiplexer_1_out), .sel(and_1_out));
  and and_1 (and_1_out, not_1_out, decoder_1_out3);
  Adder #(.width(4)) adder_1 (.a(PC_q), .b(multiplexer_1_out), .out(adder_1_out));  // open: cin, cout
  Register #(.width(4)) PC (.D(adder_1_out), .en(1'b1), .clk(clk_out), .Q(PC_q), .clr(Reset));
  Clock clk (.out(clk_out));
  Multiplexer #(.select(4), .width(8)) multiplexer_2 (
    .in0(8'h86), .in1(8'h92), .in2(8'h1), .in3(8'h90), .in4(8'ha0), .in5(8'hb1), .in6(8'h17), .in7(8'h29),
    .in8(8'hf9), .in9(8'hc3), .out(multiplexer_2_out), .sel(PC_q));  // open: in10, in11, in12, in13, in14, in15
  Decoder #(.enable("false"), .select(2)) decoder_1 (
    .out0(decoder_1_out0), .out2(decoder_1_out2), .out3(decoder_1_out3), .sel(multiplexer_2_out[7:6]));  // open: out1
  or or_1 (or_1_out, decoder_1_out3, decoder_1_out0);
  or or_2 (or_2_out, decoder_1_out0, decoder_1_out2);
  or or_3 (or_3_out, decoder_1_out0, decoder_1_out2);
  Shifter shifter_1 (
    .in({{6{1'b0}}, multiplexer_2_out[1:0]}), .\dist ({multiplexer_2_out[3:2], 1'b0}), .out(shifter_1_out));
  Decoder #(.select(2)) decoder_2 (
    .out0(decoder_2_out0), .out1(decoder_2_out1), .out2(decoder_2_out2), .out3(decoder_2_out3),
    .sel(multiplexer_2_out[5:4]), .en(or_3_out));
  Multiplexer #(.select(2), .width(8)) multiplexer_3 (
    .in0(adder_2_out), .in2(shifter_1_out), .out(multiplexer_3_out), .sel(multiplexer_2_out[7:6]));  // open: in1, in3
  and and_2 (and_2_out, or_2_out, decoder_2_out0);
  Register r0 (.D(multiplexer_3_out), .en(and_2_out), .clk(clk_out), .Q(r0_q));  // open: clr
  Multiplexer #(.select(2), .width(2)) multiplexer_4 (
    .in0(multiplexer_2_out[3:2]), .in3(2'b00), .out(multiplexer_4_out), .sel(multiplexer_2_out[7:6]));  // open: in1, in2
  Multiplexer #(.enable("true"), .select(2), .width(8)) multiplexer_5 (
    .in0(r0_q), .in1(r1_q), .in2(r2_q), .in3(r3_q), .out(multiplexer_5_out), .sel(multiplexer_4_out),
    .en(or_1_out));
  and and_3 (and_3_out, or_2_out, decoder_2_out1);
  Register r1 (.D(multiplexer_3_out), .en(and_3_out), .clk(clk_out), .Q(r1_q));  // open: clr
  Multiplexer #(.enable("true"), .select(2), .width(8)) multiplexer_6 (
    .in0(r0_q), .in1(r1_q), .in2(r2_q), .in3(r3_q), .out(multiplexer_6_out), .sel(multiplexer_2_out[1:0]),
    .en(or_1_out));
  Adder adder_2 (.a(multiplexer_6_out), .b(multiplexer_5_out), .out(adder_2_out));  // open: cin, cout
  Comparator comparator_1 (.a(multiplexer_6_out), .b(multiplexer_5_out), .eq(comparator_1_eq));  // open: gt, lt
  Register r2 (.D(multiplexer_3_out), .en(and_4_out), .clk(clk_out), .Q(r2_q));  // open: clr
  and and_4 (and_4_out, or_2_out, decoder_2_out2);
  not not_1 (not_1_out, comparator_1_eq);
  Register r3 (.D(multiplexer_3_out), .en(and_5_out), .clk(clk_out), .Q(r3_q));  // open: clr
  and and_5 (and_5_out, or_2_out, decoder_2_out3);
endmodule

module LED_sCPU (
  input  Reset
);

  wire and_1_out, and_2_out, and_3_out, and_4_out, and_5_out, and_6_out, clk_out, comparator_1_eq,
       decoder_1_out0, decoder_1_out1, decoder_1_out2, decoder_1_out3, decoder_2_out0, decoder_3_out0,
       decoder_3_out1, decoder_3_out2, decoder_3_out3, not_1_out, or_1_out, or_2_out, or_3_out;
  wire [1:0] multiplexer_4_out;
  wire [3:0] adder_1_out, multiplexer_1_out, PC_q;
  wire [7:0] adder_2_out, LED_REG_q, multiplexer_2_out, multiplexer_3_out, multiplexer_5_out,
       multiplexer_6_out, r0_q, r1_q, r2_q, r3_q, shifter_1_out;

  Multiplexer #(.width(4)) multiplexer_1 (
    .in0(4'b0001), .in1(multiplexer_2_out[5:2]), .out(multiplexer_1_out), .sel(and_1_out));
  and and_1 (and_1_out, not_1_out, decoder_1_out3);
  Adder #(.width(4)) adder_1 (.a(PC_q), .b(multiplexer_1_out), .out(adder_1_out));  // open: cin, cout
  Register #(.width(4)) PC (.D(adder_1_out), .en(1'b1), .clk(clk_out), .Q(PC_q), .clr(Reset));
  Clock clk (.out(clk_out));
  Multiplexer #(.select(4), .width(8)) multiplexer_2 (
    .in0(8'h86), .in1(8'h92), .in2(8'h1), .in3(8'h90), .in4(8'ha0), .in5(8'hb1), .in6(8'h17), .in7(8'h29),
    .in8(8'hf9), .in9(8'h68), .in10(8'hc3), .out(multiplexer_2_out), .sel(PC_q));  // open: in11, in12, in13, in14, in15
  Decoder #(.enable("false"), .select(2)) decoder_1 (
    .out0(decoder_1_out0), .out1(decoder_1_out1), .out2(decoder_1_out2), .out3(decoder_1_out3),
    .sel(multiplexer_2_out[7:6]));
  Decoder #(.select(3)) decoder_2 (
    .out0(decoder_2_out0), .sel(multiplexer_2_out[2:0]), .en(decoder_1_out1));  // open: out1, out2, out3, out4, out5, out6, out7
  or or_1 (or_1_out, decoder_1_out3, decoder_1_out1, decoder_1_out0);
  or or_2 (or_2_out, decoder_1_out0, decoder_1_out2);
  or or_3 (or_3_out, decoder_1_out0, decoder_1_out2);
  Shifter shifter_1 (
    .in({{6{1'b0}}, multiplexer_2_out[1:0]}), .\dist ({multiplexer_2_out[3:2], 1'b0}), .out(shifter_1_out));
  Decoder #(.select(2)) decoder_3 (
    .out0(decoder_3_out0), .out1(decoder_3_out1), .out2(decoder_3_out2), .out3(decoder_3_out3),
    .sel(multiplexer_2_out[5:4]), .en(or_3_out));
  Multiplexer #(.select(2), .width(8)) multiplexer_3 (
    .in0(adder_2_out), .in2(shifter_1_out), .out(multiplexer_3_out), .sel(multiplexer_2_out[7:6]));  // open: in1, in3
  and and_2 (and_2_out, or_2_out, decoder_3_out0);
  Register r0 (.D(multiplexer_3_out), .en(and_2_out), .clk(clk_out), .Q(r0_q), .clr(Reset));
  Multiplexer #(.select(2), .width(2)) multiplexer_4 (
    .in0(multiplexer_2_out[3:2]), .in1(multiplexer_2_out[5:4]), .in3(2'b00), .out(multiplexer_4_out),
    .sel(multiplexer_2_out[7:6]));  // open: in2
  Multiplexer #(.enable("true"), .select(2), .width(8)) multiplexer_5 (
    .in0(r0_q), .in1(r1_q), .in2(r2_q), .in3(r3_q), .out(multiplexer_5_out), .sel(multiplexer_4_out),
    .en(or_1_out));
  and and_3 (and_3_out, or_2_out, decoder_3_out1);
  Register r1 (.D(multiplexer_3_out), .en(and_3_out), .clk(clk_out), .Q(r1_q), .clr(Reset));
  Multiplexer #(.enable("true"), .select(2), .width(8)) multiplexer_6 (
    .in0(r0_q), .in1(r1_q), .in2(r2_q), .in3(r3_q), .out(multiplexer_6_out), .sel(multiplexer_2_out[1:0]),
    .en(or_1_out));
  Adder adder_2 (.a(multiplexer_6_out), .b(multiplexer_5_out), .out(adder_2_out));  // open: cin, cout
  Comparator comparator_1 (.a(multiplexer_6_out), .b(multiplexer_5_out), .eq(comparator_1_eq));  // open: gt, lt
  Register r2 (.D(multiplexer_3_out), .en(and_4_out), .clk(clk_out), .Q(r2_q), .clr(Reset));
  and and_4 (and_4_out, or_2_out, decoder_3_out2);
  not not_1 (not_1_out, comparator_1_eq);
  Register r3 (.D(multiplexer_3_out), .en(and_5_out), .clk(clk_out), .Q(r3_q), .clr(Reset));
  and and_5 (and_5_out, or_2_out, decoder_3_out3);
  and and_6 (and_6_out, decoder_1_out1, decoder_2_out0, multiplexer_2_out[3]);
  Register LED_REG (.D(multiplexer_5_out), .en(and_6_out), .clk(clk_out), .Q(LED_REG_q), .clr(Reset));
  // LedBar #(.inputtype("row")) ledbar_1: pin names not known; wires that end beside it: LED_REG_q

  // Notes on the sheet:
  //   rs1
  //   rs2
endmodule

module Seg_sCPU (
  input  Reset
);

  wire and_1_out, and_2_out, and_3_out, and_4_out, and_5_out, and_6_out, and_7_out, clk_out, comparator_1_eq,
       decoder_1_out0, decoder_1_out1, decoder_1_out2, decoder_1_out3, decoder_2_out0, decoder_2_out1,
       decoder_3_out0, decoder_3_out1, decoder_3_out2, decoder_3_out3, not_1_out, or_1_out, or_2_out,
       or_3_out;
  wire [1:0] multiplexer_4_out;
  wire [3:0] adder_1_out, multiplexer_1_out, PC_q;
  wire [7:0] adder_2_out, HEX_REG_q, LED_REG_q, multiplexer_2_out, multiplexer_3_out, multiplexer_5_out,
       multiplexer_6_out, r0_q, r1_q, r2_q, r3_q, shifter_1_out;

  Multiplexer #(.width(4)) multiplexer_1 (
    .in0(4'b0001), .in1(multiplexer_2_out[5:2]), .out(multiplexer_1_out), .sel(and_1_out));
  and and_1 (and_1_out, not_1_out, decoder_1_out3);
  Adder #(.width(4)) adder_1 (.a(PC_q), .b(multiplexer_1_out), .out(adder_1_out));  // open: cin, cout
  Register #(.width(4)) PC (.D(adder_1_out), .en(1'b1), .clk(clk_out), .Q(PC_q), .clr(Reset));
  Clock clk (.out(clk_out));
  Multiplexer #(.select(4), .width(8)) multiplexer_2 (
    .in0(8'h86), .in1(8'h92), .in2(8'h1), .in3(8'h90), .in4(8'ha0), .in5(8'hb1), .in6(8'h17), .in7(8'h29),
    .in8(8'hf9), .in9(8'h68), .in10(8'h69), .in11(8'hc3), .out(multiplexer_2_out), .sel(PC_q));  // open: in12, in13, in14, in15
  Decoder #(.enable("false"), .select(2)) decoder_1 (
    .out0(decoder_1_out0), .out1(decoder_1_out1), .out2(decoder_1_out2), .out3(decoder_1_out3),
    .sel(multiplexer_2_out[7:6]));
  Decoder #(.select(3)) decoder_2 (
    .out0(decoder_2_out0), .out1(decoder_2_out1), .sel(multiplexer_2_out[2:0]), .en(decoder_1_out1));  // open: out2, out3, out4, out5, out6, out7
  or or_1 (or_1_out, decoder_1_out3, decoder_1_out1, decoder_1_out0);
  or or_2 (or_2_out, decoder_1_out0, decoder_1_out2);
  or or_3 (or_3_out, decoder_1_out0, decoder_1_out2);
  Shifter shifter_1 (
    .in({{6{1'b0}}, multiplexer_2_out[1:0]}), .\dist ({multiplexer_2_out[3:2], 1'b0}), .out(shifter_1_out));
  Decoder #(.select(2)) decoder_3 (
    .out0(decoder_3_out0), .out1(decoder_3_out1), .out2(decoder_3_out2), .out3(decoder_3_out3),
    .sel(multiplexer_2_out[5:4]), .en(or_3_out));
  Multiplexer #(.select(2), .width(8)) multiplexer_3 (
    .in0(adder_2_out), .in2(shifter_1_out), .out(multiplexer_3_out), .sel(multiplexer_2_out[7:6]));  // open: in1, in3
  and and_2 (and_2_out, or_2_out, decoder_3_out0);
  Register r0 (.D(multiplexer_3_out), .en(and_2_out), .clk(clk_out), .Q(r0_q), .clr(Reset));
  Multiplexer #(.select(2), .width(2)) multiplexer_4 (
    .in0(multiplexer_2_out[3:2]), .in1(multiplexer_2_out[5:4]), .in3(2'b00), .out(multiplexer_4_out),
    .sel(multiplexer_2_out[7:6]));  // open: in2
  Multiplexer #(.enable("true"), .select(2), .width(8)) multiplexer_5 (
    .in0(r0_q), .in1(r1_q), .in2(r2_q), .in3(r3_q), .out(multiplexer_5_out), .sel(multiplexer_4_out),
    .en(or_1_out));
  and and_3 (and_3_out, or_2_out, decoder_3_out1);
  Register r1 (.D(multiplexer_3_out), .en(and_3_out), .clk(clk_out), .Q(r1_q), .clr(Reset));
  Multiplexer #(.enable("true"), .select(2), .width(8)) multiplexer_6 (
    .in0(r0_q), .in1(r1_q), .in2(r2_q), .in3(r3_q), .out(multiplexer_6_out), .sel(multiplexer_2_out[1:0]),
    .en(or_1_out));
  Adder adder_2 (.a(multiplexer_6_out), .b(multiplexer_5_out), .out(adder_2_out));  // open: cin, cout
  Comparator comparator_1 (.a(multiplexer_6_out), .b(multiplexer_5_out), .eq(comparator_1_eq));  // open: gt, lt
  Register r2 (.D(multiplexer_3_out), .en(and_4_out), .clk(clk_out), .Q(r2_q), .clr(Reset));
  and and_4 (and_4_out, or_2_out, decoder_3_out2);
  not not_1 (not_1_out, comparator_1_eq);
  Register r3 (.D(multiplexer_3_out), .en(and_5_out), .clk(clk_out), .Q(r3_q), .clr(Reset));
  and and_5 (and_5_out, or_2_out, decoder_3_out3);
  and and_6 (and_6_out, decoder_1_out1, decoder_2_out0, multiplexer_2_out[3]);
  Register LED_REG (.D(multiplexer_5_out), .en(and_6_out), .clk(clk_out), .Q(LED_REG_q), .clr(Reset));
  and and_7 (and_7_out, decoder_1_out1, decoder_2_out1, multiplexer_2_out[3]);
  Register HEX_REG (.D(multiplexer_5_out), .en(and_7_out), .clk(clk_out), .Q(HEX_REG_q), .clr(Reset));
  // LedBar #(.inputtype("row")) ledbar_1: pin names not known; wires that end beside it: LED_REG_q
  Hex_Digit_Display #(.decimalPoint("false")) hex_digit_display_1 (.value(HEX_REG_q[7:4]));
  Hex_Digit_Display #(.decimalPoint("false")) hex_digit_display_2 (.value(HEX_REG_q[3:0]));

  // Notes on the sheet:
  //   rs1
  //   rs2
endmodule

module Switch_sCPU (
  input  Reset
);

  wire and_1_out, and_2_out, and_3_out, and_4_out, and_5_out, and_6_out, and_7_out, and_8_out, clk_out,
       comparator_1_eq, decoder_1_out0, decoder_1_out1, decoder_1_out2, decoder_1_out3, decoder_2_out0,
       decoder_2_out1, decoder_3_out0, decoder_3_out1, decoder_3_out2, decoder_3_out3, not_1_out, or_1_out,
       or_2_out, or_3_out;
  wire [1:0] multiplexer_2_out, multiplexer_2_out_2, multiplexer_2_out_3, multiplexer_2_out_4,
       multiplexer_5_out;
  wire [3:0] adder_1_out, multiplexer_1_out, PC_q;
  wire [7:0] adder_2_out, dipswitch_1_p1, HEX_REG_q, LED_REG_q, multiplexer_3_out, multiplexer_4_out,
       multiplexer_6_out, multiplexer_7_out, r0_q, r1_q, r2_q, r3_q, shifter_1_out;

  Multiplexer #(.width(4)) multiplexer_1 (
    .in0(4'b0001), .in1({multiplexer_2_out_2, multiplexer_2_out}), .out(multiplexer_1_out), .sel(and_1_out));
  and and_1 (and_1_out, not_1_out, decoder_1_out3);
  Adder #(.width(4)) adder_1 (.a(PC_q), .b(multiplexer_1_out), .out(adder_1_out));  // open: cin, cout
  Clock clk (.out(clk_out));
  Register #(.width(4)) PC (.D(adder_1_out), .en(1'b1), .clk(clk_out), .Q(PC_q), .clr(Reset));
  Multiplexer #(.select(4), .width(8)) multiplexer_2 (
    .in0(8'h40), .in1(8'h90), .in2(8'ha0), .in3(8'hb1), .in4(8'h17), .in5(8'h29), .in6(8'hf9), .in7(8'h68),
    .in8(8'h69), .in9(8'hc3),
    .out({multiplexer_2_out_3, multiplexer_2_out_2, multiplexer_2_out, multiplexer_2_out_4}), .sel(PC_q));  // open: in10, in11, in12, in13, in14, in15
  Multiplexer #(.enable("true"), .select(3), .width(8)) multiplexer_3 (
    .in0(dipswitch_1_p1), .out(multiplexer_3_out), .sel({multiplexer_2_out[0], multiplexer_2_out_4}),
    .en(decoder_1_out1));  // open: in1, in2, in3, in4, in5, in6, in7
  Decoder #(.enable("false"), .select(2)) decoder_1 (
    .out0(decoder_1_out0), .out1(decoder_1_out1), .out2(decoder_1_out2), .out3(decoder_1_out3),
    .sel(multiplexer_2_out_3));
  Decoder #(.select(3)) decoder_2 (
    .out0(decoder_2_out0), .out1(decoder_2_out1), .sel({multiplexer_2_out[0], multiplexer_2_out_4}),
    .en(decoder_1_out1));  // open: out2, out3, out4, out5, out6, out7
  or or_1 (or_1_out, decoder_1_out3, decoder_1_out1, decoder_1_out0);
  and and_2 (and_2_out, decoder_1_out1, ~multiplexer_2_out[1]);  // AND_Gate
  Shifter shifter_1 (.in({{6{1'b0}}, multiplexer_2_out_4}), .\dist ({multiplexer_2_out, 1'b0}), .out(shifter_1_out));
  or or_2 (or_2_out, decoder_1_out0, and_2_out, decoder_1_out2);
  or or_3 (or_3_out, decoder_1_out0, and_2_out, decoder_1_out2);
  Decoder #(.select(2)) decoder_3 (
    .out0(decoder_3_out0), .out1(decoder_3_out1), .out2(decoder_3_out2), .out3(decoder_3_out3),
    .sel(multiplexer_2_out_2), .en(or_3_out));
  Multiplexer #(.select(2), .width(8)) multiplexer_4 (
    .in0(adder_2_out), .in1(multiplexer_3_out), .in2(shifter_1_out), .out(multiplexer_4_out),
    .sel(multiplexer_2_out_3));  // open: in3
  Register r0 (.D(multiplexer_4_out), .en(and_3_out), .clk(clk_out), .Q(r0_q), .clr(Reset));
  and and_3 (and_3_out, or_2_out, decoder_3_out0);
  Multiplexer #(.select(2), .width(2)) multiplexer_5 (
    .in0(multiplexer_2_out), .in1(multiplexer_2_out_2), .in3(2'b00), .out(multiplexer_5_out),
    .sel(multiplexer_2_out_3));  // open: in2
  Multiplexer #(.enable("true"), .select(2), .width(8)) multiplexer_6 (
    .in0(r0_q), .in1(r1_q), .in2(r2_q), .in3(r3_q), .out(multiplexer_6_out), .sel(multiplexer_5_out),
    .en(or_1_out));
  and and_4 (and_4_out, or_2_out, decoder_3_out1);
  Register r1 (.D(multiplexer_4_out), .en(and_4_out), .clk(clk_out), .Q(r1_q), .clr(Reset));
  Multiplexer #(.enable("true"), .select(2), .width(8)) multiplexer_7 (
    .in0(r0_q), .in1(r1_q), .in2(r2_q), .in3(r3_q), .out(multiplexer_7_out), .sel(multiplexer_2_out_4),
    .en(or_1_out));
  Adder adder_2 (.a(multiplexer_7_out), .b(multiplexer_6_out), .out(adder_2_out));  // open: cin, cout
  Comparator comparator_1 (.a(multiplexer_7_out), .b(multiplexer_6_out), .eq(comparator_1_eq));  // open: gt, lt
  and and_5 (and_5_out, or_2_out, decoder_3_out2);
  not not_1 (not_1_out, comparator_1_eq);
  Register r2 (.D(multiplexer_4_out), .en(and_5_out), .clk(clk_out), .Q(r2_q), .clr(Reset));
  and and_6 (and_6_out, or_2_out, decoder_3_out3);
  Register r3 (.D(multiplexer_4_out), .en(and_6_out), .clk(clk_out), .Q(r3_q), .clr(Reset));
  and and_7 (and_7_out, decoder_1_out1, decoder_2_out0, multiplexer_2_out[1]);
  Register LED_REG (.D(multiplexer_6_out), .en(and_7_out), .clk(clk_out), .Q(LED_REG_q), .clr(Reset));
  and and_8 (and_8_out, decoder_1_out1, decoder_2_out1, multiplexer_2_out[1]);
  Register HEX_REG (.D(multiplexer_6_out), .en(and_8_out), .clk(clk_out), .Q(HEX_REG_q), .clr(Reset));
  // DipSwitch dipswitch_1: pin names not known; wires that end beside it: dipswitch_1_p1[0], dipswitch_1_p1[1], dipswitch_1_p1[2], dipswitch_1_p1[3], dipswitch_1_p1[4], dipswitch_1_p1[5], dipswitch_1_p1[6], dipswitch_1_p1[7]
  // LedBar #(.inputtype("row")) ledbar_1: pin names not known; wires that end beside it: LED_REG_q
  Hex_Digit_Display #(.decimalPoint("false")) hex_digit_display_1 (.value(HEX_REG_q[7:4]));
  Hex_Digit_Display #(.decimalPoint("false")) hex_digit_display_2 (.value(HEX_REG_q[3:0]));

  // Notes on the sheet:
  //   input
  //   output
  //   rs1
  //   rs2
endmodule

module Button_sCPU (
  input  Reset
);

  wire and_1_out, and_2_out, and_3_out, and_4_out, and_5_out, and_6_out, and_7_out, and_8_out, clk_out,
       comparator_1_eq, decoder_1_out0, decoder_1_out1, decoder_1_out2, decoder_1_out3, decoder_2_out0,
       decoder_2_out1, decoder_3_out0, decoder_3_out1, decoder_3_out2, decoder_3_out3, not_1_out, or_1_out,
       or_2_out, or_3_out;
  wire [1:0] multiplexer_2_out, multiplexer_2_out_2, multiplexer_2_out_3, multiplexer_2_out_4,
       multiplexer_5_out;
  wire [3:0] adder_1_out, multiplexer_1_out, PC_q;
  wire [7:0] adder_2_out, button_1_out, dipswitch_1_p1, HEX_REG_q, LED_REG_q, multiplexer_3_out,
       multiplexer_4_out, multiplexer_6_out, multiplexer_7_out, r0_q, r1_q, r2_q, r3_q, shifter_1_out;

  Multiplexer #(.width(4)) multiplexer_1 (
    .in0(4'b0001), .in1({multiplexer_2_out_2, multiplexer_2_out}), .out(multiplexer_1_out), .sel(and_1_out));
  and and_1 (and_1_out, not_1_out, decoder_1_out3);
  Adder #(.width(4)) adder_1 (.a(PC_q), .b(multiplexer_1_out), .out(adder_1_out));  // open: cin, cout
  Clock clk (.out(clk_out));
  Register #(.width(4)) PC (.D(adder_1_out), .en(1'b1), .clk(clk_out), .Q(PC_q), .clr(Reset));
  Multiplexer #(.select(4), .width(8)) multiplexer_2 (
    .in0(8'h40), .in1(8'h90), .in2(8'ha0), .in3(8'hb1), .in4(8'h17), .in5(8'h29), .in6(8'h58), .in7(8'hf5),
    .in8(8'h90), .in9(8'h41), .in10(8'hc9), .in11(8'hfb), .in12(8'h69), .in13(8'hc1),
    .out({multiplexer_2_out_3, multiplexer_2_out_2, multiplexer_2_out, multiplexer_2_out_4}), .sel(PC_q));  // open: in14, in15
  Multiplexer #(.enable("true"), .select(3), .width(8)) multiplexer_3 (
    .in0(dipswitch_1_p1), .in1(button_1_out), .out(multiplexer_3_out),
    .sel({multiplexer_2_out[0], multiplexer_2_out_4}), .en(decoder_1_out1));  // open: in2, in3, in4, in5, in6, in7
  Decoder #(.enable("false"), .select(2)) decoder_1 (
    .out0(decoder_1_out0), .out1(decoder_1_out1), .out2(decoder_1_out2), .out3(decoder_1_out3),
    .sel(multiplexer_2_out_3));
  Decoder #(.select(3)) decoder_2 (
    .out0(decoder_2_out0), .out1(decoder_2_out1), .sel({multiplexer_2_out[0], multiplexer_2_out_4}),
    .en(decoder_1_out1));  // open: out2, out3, out4, out5, out6, out7
  or or_1 (or_1_out, decoder_1_out3, decoder_1_out1, decoder_1_out0);
  and and_2 (and_2_out, decoder_1_out1, ~multiplexer_2_out[1]);  // AND_Gate
  Shifter shifter_1 (.in({{6{1'b0}}, multiplexer_2_out_4}), .\dist ({multiplexer_2_out, 1'b0}), .out(shifter_1_out));
  or or_2 (or_2_out, decoder_1_out0, and_2_out, decoder_1_out2);
  or or_3 (or_3_out, decoder_1_out0, and_2_out, decoder_1_out2);
  Decoder #(.select(2)) decoder_3 (
    .out0(decoder_3_out0), .out1(decoder_3_out1), .out2(decoder_3_out2), .out3(decoder_3_out3),
    .sel(multiplexer_2_out_2), .en(or_3_out));
  Multiplexer #(.select(2), .width(8)) multiplexer_4 (
    .in0(adder_2_out), .in1(multiplexer_3_out), .in2(shifter_1_out), .out(multiplexer_4_out),
    .sel(multiplexer_2_out_3));  // open: in3
  Register r0 (.D(multiplexer_4_out), .en(and_3_out), .clk(clk_out), .Q(r0_q), .clr(Reset));
  and and_3 (and_3_out, or_2_out, decoder_3_out0);
  Multiplexer #(.select(2), .width(2)) multiplexer_5 (
    .in0(multiplexer_2_out), .in1(multiplexer_2_out_2), .in3(2'b00), .out(multiplexer_5_out),
    .sel(multiplexer_2_out_3));  // open: in2
  Multiplexer #(.enable("true"), .select(2), .width(8)) multiplexer_6 (
    .in0(r0_q), .in1(r1_q), .in2(r2_q), .in3(r3_q), .out(multiplexer_6_out), .sel(multiplexer_5_out),
    .en(or_1_out));
  and and_4 (and_4_out, or_2_out, decoder_3_out1);
  Register r1 (.D(multiplexer_4_out), .en(and_4_out), .clk(clk_out), .Q(r1_q), .clr(Reset));
  Multiplexer #(.enable("true"), .select(2), .width(8)) multiplexer_7 (
    .in0(r0_q), .in1(r1_q), .in2(r2_q), .in3(r3_q), .out(multiplexer_7_out), .sel(multiplexer_2_out_4),
    .en(or_1_out));
  Adder adder_2 (.a(multiplexer_7_out), .b(multiplexer_6_out), .out(adder_2_out));  // open: cin, cout
  Comparator comparator_1 (.a(multiplexer_7_out), .b(multiplexer_6_out), .eq(comparator_1_eq));  // open: gt, lt
  and and_5 (and_5_out, or_2_out, decoder_3_out2);
  not not_1 (not_1_out, comparator_1_eq);
  Register r2 (.D(multiplexer_4_out), .en(and_5_out), .clk(clk_out), .Q(r2_q), .clr(Reset));
  and and_6 (and_6_out, or_2_out, decoder_3_out3);
  Register r3 (.D(multiplexer_4_out), .en(and_6_out), .clk(clk_out), .Q(r3_q), .clr(Reset));
  and and_7 (and_7_out, decoder_1_out1, decoder_2_out0, multiplexer_2_out[1]);
  Register LED_REG (.D(multiplexer_6_out), .en(and_7_out), .clk(clk_out), .Q(LED_REG_q), .clr(Reset));
  and and_8 (and_8_out, decoder_1_out1, decoder_2_out1, multiplexer_2_out[1]);
  Button button_1 (.out(button_1_out[0]));
  Button button_2 (.out(button_1_out[1]));
  Button button_3 (.out(button_1_out[2]));
  Button button_4 (.out(button_1_out[3]));
  Button button_5 (.out(button_1_out[4]));
  Button button_6 (.out(button_1_out[5]));
  Button button_7 (.out(button_1_out[6]));
  Button button_8 (.out(button_1_out[7]));
  Register HEX_REG (.D(multiplexer_6_out), .en(and_8_out), .clk(clk_out), .Q(HEX_REG_q), .clr(Reset));
  // DipSwitch dipswitch_1: pin names not known; wires that end beside it: dipswitch_1_p1[0], dipswitch_1_p1[1], dipswitch_1_p1[2], dipswitch_1_p1[3], dipswitch_1_p1[4], dipswitch_1_p1[5], dipswitch_1_p1[6], dipswitch_1_p1[7]
  // LedBar #(.inputtype("row")) ledbar_1: pin names not known; wires that end beside it: LED_REG_q
  Hex_Digit_Display #(.decimalPoint("false")) hex_digit_display_1 (.value(HEX_REG_q[7:4]));
  Hex_Digit_Display #(.decimalPoint("false")) hex_digit_display_2 (.value(HEX_REG_q[3:0]));

  // Notes on the sheet:
  //   input
  //   output
  //   rs1
  //   rs2
endmodule
